// Logisim project pacman.circ as structural Verilog: 16 circuits, main circuit test
module sprite_dict (
  input  [4:0] in_1,
  output [2:0] out_2,
  output [2:0] out_3,
  output [2:0] out_4
);

  wire [8:0] rom_1_data;

  ROM #(.addrWidth(5), .dataWidth(9)) rom_1 (.addr(in_1), .data(rom_1_data));  // open: sel
  nine_to_3x3 nine_to_3x3_1 (.in_1(rom_1_data), .out_2(out_2), .out_3(out_3), .out_4(out_4));

  // Notes on the sheet:
  //   SPRITE DICTIONARY
  //   contents of rom_1 (hex, n*v repeats v):
  //   e3 18e 16a ad bf 13b 28 10 38 92 b0 32 1a 98 90 12 30 18 9a b8 b2 3a ba
endmodule

module map_handler (
  input  [5:0] x,
  input  [5:0] y,
  output [4:0] out_3
);

  wire [8:0] adder_1_out, bit_extender_1_out, bit_extender_2_out, multiplier_1_out;

  assign bit_extender_1_out = {{3{1'b0}}, y};  // Bit_Extender bit_extender_1
  assign bit_extender_2_out = {{3{1'b0}}, x};  // Bit_Extender bit_extender_2
  Adder #(.width(9)) adder_1 (.a(bit_extender_2_out), .b(multiplier_1_out), .out(adder_1_out));  // open: cin, cout
  Multiplier #(.width(9)) multiplier_1 (.a(bit_extender_1_out), .b(9'h14), .out(multiplier_1_out));  // open: cin, cout
  ROM #(.addrWidth(9), .dataWidth(5)) rom_1 (.addr(adder_1_out), .data(out_3));  // open: sel

  // Notes on the sheet:
  //   MAP HANDLER
  //   contents of rom_1 (hex, n*v repeats v):
  //   17 c 7*8 15 15 7*8 b 17 17 9 7*7 9 9 7*7 9 17 17 9 17 11 10 7 11 10 7 d a 7 11 10 7 11 10 17 9 17 17
  //   9 16*7 9 17 17 9 7 11 10 7 f 7 11 15 15 10 7 f 7 11 10 7 9 17 17 9 4*7 9 7 7 9 9 7 7 9 4*7 9 17 17 d
  //   8 8 b 7 12 10 17 d a 17 11 14 7 c 8 8 a 5*17 9 7 9 6*17 9 7 9 4*17 4*8 a 7 e 17 c 17 17 b 17 e 7 d
  //   4*8 5*17 7 17 17 9 17 17 9 17 17 7 10*17 7 17 17 9 17 17 9 17 17 7 5*17 4*8 b 7 f 17 d 8 8 a 17 f 7
  //   c 4*8 4*17 9 7 9 6*17 9 7 9 5*17 c 8 8 a 7 12 10 17 c b 17 11 14 7 d 8 8 b 17 17 9 4*7 9 7 7 9 9 7 7
  //   9 4*7 9 17 17 9 7 11 10 7 e 7 11 13 13 10 7 e 7 11 10 7 9 17 17 9 16*7 9 17 17 9 17 11 10 7 11 10 7
  //   c b 7 11 10 7 11 10 17 9 17 17 9 7*7 9 9 7*7 9 17 17 d 7*8 13 13 7*8 a 17
endmodule

module get_next_sprite (
  input  [29:0] sprite_reg,
  input  [29:0] sprite_reg_2,
  input  [29:0] sprite_reg_3,
  input  [4:0] x,
  output [29:0] out_5,
  output [29:0] out_6,
  output [29:0] out_7
);

  wire [4:0] multiplier_1_out;
  wire [29:0] bit_extender_1_out, shifter_1_out;

  assign out_5 = sprite_reg & shifter_1_out;  // AND_Gate and_1, 30 bits wide
  assign bit_extender_1_out = {{27{1'b0}}, 3'b111};  // Bit_Extender bit_extender_1
  Shifter #(.width(30)) shifter_1 (.in(bit_extender_1_out), .\dist (multiplier_1_out), .out(shifter_1_out));
  Multiplier #(.width(5)) multiplier_1 (.a(x), .b(5'b00011), .out(multiplier_1_out));  // open: cin, cout
  assign out_6 = sprite_reg_2 & shifter_1_out;  // AND_Gate and_2, 30 bits wide
  assign out_7 = sprite_reg_3 & shifter_1_out;  // AND_Gate and_3, 30 bits wide

  // Notes on the sheet:
  //   NEXT SPRITE SUB
endmodule

module nine_to_3x3 (
  input  [8:0] in_1,
  output [2:0] out_2,
  output [2:0] out_3,
  output [2:0] out_4
);


  assign out_2 = in_1[8:6];
  assign out_3 = in_1[5:3];
  assign out_4 = in_1[2:0];

  // Notes on the sheet:
  //   9 -> 3x3
endmodule

module player (
  input  [5:0] g_x,
  input  [5:0] g_y,
  input  [2:0] in_3,
  input  [6:0] in_4,
  input  [2:0] in_5,
  input  in_6,
  input  reset,
  input  [2:0] in_8,
  input  clock,
  input  [2:0] in_10,
  input  [2:0] in_11,
  input  [2:0] in_12,
  input  loaded,
  output out_14,
  output [8:0] out_15,
  output out_16,
  output out_17,
  output out_18,
  output [4:0] player,
  output fruit,
  output [5:0] out_21,
  output [5:0] out_22
);

  wire and_1_out, any_x, any_y, clk, collision, comparator_1_eq, comparator_2_eq, comparator_3_eq,
       comparator_4_eq, comparator_5_eq, comparator_6_eq, comparator_7_eq, comparator_8_eq, comparator_9_eq,
       comparator_10_eq, comparator_11_eq, controlled_buffer_1_out, controlled_buffer_2_out,
       controlled_buffer_3_out, controlled_buffer_4_out, controlled_buffer_9_out, not_1_out, not_2_out,
       not_3_out, or_1_out, or_3_out, or_5_out, or_6_out, transistor_2_out, transistor_4_out,
       transistor_6_out, transistor_7_out, x_inc, y_inc;
  wire [2:0] controlled_buffer_11_out, or_9_out, or_10_out, or_11_out;
  wire [4:0] controlled_buffer_5_out;
  wire [5:0] x_q, y_q;
  wire [6:0] register_1_q;
  wire [8:0] adder_3_out, bit_extender_1_out, bit_extender_2_out, multiplier_1_out;

  any_collision_detector any_collision_detector_1 (
    .x(out_22), .y(out_21), .x_inc(x_inc), .y_inc(y_inc), .any_x(any_x), .any_y(any_y), .out_7(collision));  // open: out_8, out_9
  Register #(.width(7)) register_1 (.D(in_4), .Q(register_1_q), .clk(in_6), .clr(reset));  // open: en
  or or_1 (or_1_out, out_14, ~loaded);  // OR_Gate
  Transistor transistor_1 (.in(clock), .out(clk), .gate(or_1_out));
  Comparator #(.width(7)) comparator_1 (.a(register_1_q), .b(7'b1000110), .eq(comparator_1_eq));  // open: gt, lt
  Comparator #(.width(7)) comparator_2 (.a(register_1_q), .b(7'b1110111), .eq(comparator_2_eq));  // open: gt, lt
  Comparator #(.width(7)) comparator_3 (.a(register_1_q), .b(7'b1001011), .eq(comparator_3_eq));  // open: gt, lt
  Comparator #(.width(7)) comparator_4 (.a(register_1_q), .b(7'b1110011), .eq(comparator_4_eq));  // open: gt, lt
  Comparator #(.width(7)) comparator_5 (.a(register_1_q), .b(7'b0110010), .eq(comparator_5_eq));  // open: gt, lt
  Comparator #(.width(7)) comparator_6 (.a(register_1_q), .b(7'b1100100), .eq(comparator_6_eq));  // open: gt, lt
  Comparator #(.width(7)) comparator_7 (.a(register_1_q), .b(7'b1000100), .eq(comparator_7_eq));  // open: gt, lt
  Comparator #(.width(7)) comparator_8 (.a(register_1_q), .b(7'b1100001), .eq(comparator_8_eq));  // open: gt, lt
  assign controlled_buffer_1_out = any_x ? controlled_buffer_2_out : 1'bz;  // Controlled_Buffer controlled_buffer_1
  assign controlled_buffer_2_out = collision ? clk : 1'bz;  // Controlled_Buffer controlled_buffer_2
  assign controlled_buffer_3_out = collision ? clk : 1'bz;  // Controlled_Buffer controlled_buffer_3
  assign controlled_buffer_4_out = any_y ? controlled_buffer_3_out : 1'bz;  // Controlled_Buffer controlled_buffer_4
  or or_2 (y_inc, comparator_1_eq, comparator_2_eq);
  or or_3 (or_3_out, comparator_3_eq, comparator_4_eq);
  or or_4 (x_inc, comparator_5_eq, comparator_6_eq);
  or or_5 (or_5_out, comparator_7_eq, comparator_8_eq);
  Transistor transistor_2 (.in(controlled_buffer_1_out), .out(transistor_2_out), .gate(reset));
  Transistor #(.\type ("n")) transistor_3 (.in(clk), .out(transistor_2_out), .gate(reset));
  Transistor transistor_4 (.in(controlled_buffer_4_out), .out(transistor_4_out), .gate(reset));
  Transistor #(.\type ("n")) transistor_5 (.in(clk), .out(transistor_4_out), .gate(reset));
  assign controlled_buffer_5_out = y_inc ? 5'b00010 : 5'bz;  // Controlled_Buffer controlled_buffer_5
  assign controlled_buffer_5_out = or_3_out ? 5'b00011 : 5'bz;  // Controlled_Buffer controlled_buffer_6
  assign controlled_buffer_5_out = x_inc ? 5'b00001 : 5'bz;  // Controlled_Buffer controlled_buffer_7
  assign controlled_buffer_5_out = or_5_out ? {5{1'b0}} : 5'bz;  // Controlled_Buffer controlled_buffer_8
  Transistor transistor_6 (.in(x_inc), .out(transistor_6_out), .gate(reset));
  Pull_Resistor #(.pull(1)) pull_resistor_1 (.node(transistor_6_out));
  not not_1 (not_1_out, reset);
  Transistor transistor_7 (.in(y_inc), .out(transistor_7_out), .gate(reset));
  Pull_Resistor #(.pull(1)) pull_resistor_2 (.node(transistor_7_out));
  not not_2 (not_2_out, reset);
  Pull_Resistor pull_resistor_3 (.node(x_inc));
  Pull_Resistor pull_resistor_4 (.node(or_5_out));
  or or_6 (or_6_out, or_5_out, x_inc, or_3_out, y_inc);
  Counter #(.width(6), .max('h11)) x (
    .load(transistor_6_out), .D(6'b001010), .count(not_1_out), .Q(x_q), .clk(transistor_2_out));  // open: carry, clr
  Counter #(.width(6), .max('h11)) y (
    .load(transistor_7_out), .D(6'b001010), .count(not_2_out), .Q(y_q), .clk(transistor_4_out));  // open: carry, clr
  or or_7 (any_y, y_inc, or_3_out);
  Pull_Resistor pull_resistor_5 (.node(y_inc));
  Pull_Resistor pull_resistor_6 (.node(or_3_out));
  Register #(.width(5)) register_2 (
    .D(controlled_buffer_5_out), .Q(player), .clk(controlled_buffer_9_out));  // open: en, clr
  assign controlled_buffer_9_out = or_6_out ? clk : 1'bz;  // Controlled_Buffer controlled_buffer_9
  Adder #(.width(6)) adder_1 (.a(x_q), .b(6'b000001), .out(out_22));  // open: cin, cout
  assign bit_extender_1_out = {{3{1'b0}}, out_22};  // Bit_Extender bit_extender_1
  Adder #(.width(6)) adder_2 (.a(6'b000001), .b(y_q), .out(out_21));  // open: cin, cout
  assign bit_extender_2_out = {{3{1'b0}}, out_21};  // Bit_Extender bit_extender_2
  or or_8 (any_x, x_inc, or_5_out);
  Adder #(.width(9)) adder_3 (.a(bit_extender_1_out), .b(multiplier_1_out), .out(adder_3_out));  // open: cin, cout
  Multiplier #(.width(9)) multiplier_1 (.a(9'h14), .b(bit_extender_2_out), .out(multiplier_1_out));  // open: cin, cout
  assign out_15 = clk ? adder_3_out : 9'bz;  // Controlled_Buffer controlled_buffer_10
  Pull_Resistor pull_resistor_7 (.node(out_15));
  Comparator #(.width(6), .mode("unsigned")) comparator_9 (.a(g_x), .b(out_22), .eq(comparator_9_eq));  // open: gt, lt
  Comparator #(.width(6), .mode("unsigned")) comparator_10 (
    .a(g_y), .b(out_21), .eq(comparator_10_eq));  // open: gt, lt
  assign or_9_out = in_3 | in_5 | in_8;  // OR_Gate or_9, 3 bits wide
  assign or_10_out = in_10 | in_11 | in_12;  // OR_Gate or_10, 3 bits wide
  Counter #(.width(1), .max('h1), .ongoal("stay")) counter_1 (
    .Q(out_14), .clk(and_1_out), .clr(reset));  // open: load, D, count, carry
  and and_1 (and_1_out, comparator_9_eq, comparator_10_eq);
  not not_3 (not_3_out, loaded);
  assign controlled_buffer_11_out = not_3_out ? or_11_out : 3'bz;  // Controlled_Buffer controlled_buffer_11
  assign or_11_out = or_9_out | or_10_out;  // OR_Gate or_11, 3 bits wide
  Comparator #(.width(3)) comparator_11 (
    .a(controlled_buffer_11_out), .b(3'b010), .eq(comparator_11_eq));  // open: gt, lt
  Pull_Resistor pull_resistor_8 (.node(comparator_11_eq));
  Pull_Resistor pull_resistor_9 (.node(out_14));
  Counter #(.width(32), .max('hffffffff), .trigger("falling")) counter_2 (
    .carry(out_18), .clk(comparator_11_eq), .clr(reset));  // open: load, D, count, Q

  assign fruit = 1'b0;
  assign out_16 = in_6;
  assign out_17 = 1'b1;

  // Other names for the same wires on the sheet: coll = out_14; x[5:0] = out_22; y[5:0] = out_21

  // Notes on the sheet:
  //   collision detector
  //   xy position
  //   main
  //   PLAYER
  //   ghost collision
  //   current tile input
endmodule

module collision_detector (
  input  [4:0] in_1,
  output out_2
);

  wire comparator_1_eq, not_1_out;
  wire [4:0] controlled_buffer_1_out;

  or or_1 (out_2, controlled_buffer_1_out[4], controlled_buffer_1_out[3]);
  assign controlled_buffer_1_out = not_1_out ? in_1 : 5'bz;  // Controlled_Buffer controlled_buffer_1
  Pull_Resistor pull_resistor_1 (.node(controlled_buffer_1_out));
  not not_1 (not_1_out, comparator_1_eq);
  Comparator #(.width(5), .mode("unsigned")) comparator_1 (
    .a(5'b10111), .b(in_1), .eq(comparator_1_eq));  // open: gt, lt

  // Notes on the sheet:
  //   COLLISION
endmodule

// 0xf
module current_mode (
  input  reset,
  input  fruit,
  input  clk,
  output hunt,
  output scatter
);

  wire controlled_buffer_1_out, controlled_buffer_2_out, controlled_buffer_3_out, counter_1_carry,
       counter_2_carry, counter_3_carry, counter_4_carry, not_1_out, not_2_out, or_1_out, or_2_out, or_3_out,
       t_ff_1_q, t_ff_1_qn;

  assign controlled_buffer_1_out = t_ff_1_q ? counter_1_carry : 1'bz;  // Controlled_Buffer controlled_buffer_1
  Counter #(.width(12), .max('hf)) counter_1 (
    .carry(counter_1_carry), .clk(controlled_buffer_2_out), .clr(reset));  // open: load, D, count, Q
  assign controlled_buffer_2_out = not_1_out ? clk : 1'bz;  // Controlled_Buffer controlled_buffer_2
  not not_1 (not_1_out, fruit);
  assign controlled_buffer_3_out = scatter ? counter_1_carry : 1'bz;  // Controlled_Buffer controlled_buffer_3
  or or_1 (or_1_out, reset, counter_2_carry);
  Counter #(.width(5), .max('h14)) counter_2 (
    .carry(counter_2_carry), .clk(controlled_buffer_1_out), .clr(or_1_out));  // open: load, D, count, Q
  or or_2 (or_2_out, counter_2_carry, counter_3_carry);
  assign scatter = not_2_out ? t_ff_1_qn : 1'bz;  // Controlled_Buffer controlled_buffer_4
  not not_2 (not_2_out, counter_4_carry);
  or or_3 (or_3_out, counter_3_carry, reset);
  Counter #(.width(5), .max('h7)) counter_3 (
    .carry(counter_3_carry), .clk(controlled_buffer_3_out), .clr(or_3_out));  // open: load, D, count, Q
  Counter #(.width(2), .max('h3)) counter_4 (
    .carry(counter_4_carry), .clk(t_ff_1_qn), .clr(reset));  // open: load, D, count, Q
  T_Flip_Flop t_ff_1 (.clk(or_2_out), .T(or_2_out), .Q(t_ff_1_q), .Qn(t_ff_1_qn), .reset(reset));  // open: preset, en
  Pull_Resistor pull_resistor_1 (.node(scatter));
  or or_4 (hunt, t_ff_1_q, counter_4_carry);

  // Notes on the sheet:
  //   GHOST MODE
endmodule

module test (
);

  wire button_1_out, intel_core_pentium_1_clock, intel_core_pentium_1_draw, intel_core_pentium_1_loaded,
       intel_core_pentium_1_out_16, intel_core_pentium_1_out_17, intel_core_pentium_1_out_18,
       intel_core_pentium_1_out_19, intel_core_pentium_1_out_20, intel_core_pentium_1_pacman,
       keyboard_1_avail;
  wire [2:0] test_video_chip_1_out_135, test_video_chip_1_out_136, test_video_chip_1_out_137,
       test_video_chip_1_out_138, test_video_chip_1_out_139, test_video_chip_1_out_140;
  wire [6:0] keyboard_1_data;
  wire [8:0] intel_core_pentium_1_index;
  wire [15:0] intel_core_pentium_1_data;
  wire [29:0] test_video_chip_1_out_10, test_video_chip_1_out_11, test_video_chip_1_out_12,
       test_video_chip_1_out_13, test_video_chip_1_out_14, test_video_chip_1_out_15,
       test_video_chip_1_out_16, test_video_chip_1_out_17, test_video_chip_1_out_18,
       test_video_chip_1_out_19, test_video_chip_1_out_20, test_video_chip_1_out_21,
       test_video_chip_1_out_22, test_video_chip_1_out_23, test_video_chip_1_out_24,
       test_video_chip_1_out_25, test_video_chip_1_out_26, test_video_chip_1_out_27,
       test_video_chip_1_out_28, test_video_chip_1_out_29, test_video_chip_1_out_30,
       test_video_chip_1_out_31, test_video_chip_1_out_32, test_video_chip_1_out_33,
       test_video_chip_1_out_34, test_video_chip_1_out_35, test_video_chip_1_out_36,
       test_video_chip_1_out_37, test_video_chip_1_out_38, test_video_chip_1_out_39,
       test_video_chip_1_out_40, test_video_chip_1_out_41, test_video_chip_1_out_42,
       test_video_chip_1_out_43, test_video_chip_1_out_44, test_video_chip_1_out_45,
       test_video_chip_1_out_46, test_video_chip_1_out_47, test_video_chip_1_out_48,
       test_video_chip_1_out_49, test_video_chip_1_out_50, test_video_chip_1_out_51,
       test_video_chip_1_out_52, test_video_chip_1_out_53, test_video_chip_1_out_54,
       test_video_chip_1_out_55, test_video_chip_1_out_56, test_video_chip_1_out_57,
       test_video_chip_1_out_58, test_video_chip_1_out_59, test_video_chip_1_out_60,
       test_video_chip_1_out_61, test_video_chip_1_out_62, test_video_chip_1_out_63,
       test_video_chip_1_out_64, test_video_chip_1_out_65, test_video_chip_1_out_66,
       test_video_chip_1_out_67, test_video_chip_1_out_68, test_video_chip_1_out_69,
       test_video_chip_1_out_70, test_video_chip_1_out_71, test_video_chip_1_out_72,
       test_video_chip_1_out_73, test_video_chip_1_out_74, test_video_chip_1_out_75,
       test_video_chip_1_out_76, test_video_chip_1_out_77, test_video_chip_1_out_78,
       test_video_chip_1_out_79, test_video_chip_1_out_80, test_video_chip_1_out_81,
       test_video_chip_1_out_82, test_video_chip_1_out_83, test_video_chip_1_out_84,
       test_video_chip_1_out_85, test_video_chip_1_out_86, test_video_chip_1_out_87,
       test_video_chip_1_out_88, test_video_chip_1_out_89, test_video_chip_1_out_90,
       test_video_chip_1_out_91, test_video_chip_1_out_92, test_video_chip_1_out_93,
       test_video_chip_1_out_94, test_video_chip_1_out_95, test_video_chip_1_out_96,
       test_video_chip_1_out_97, test_video_chip_1_out_98, test_video_chip_1_out_99,
       test_video_chip_1_out_100, test_video_chip_1_out_101, test_video_chip_1_out_102,
       test_video_chip_1_out_103, test_video_chip_1_out_104, test_video_chip_1_out_105,
       test_video_chip_1_out_106, test_video_chip_1_out_107, test_video_chip_1_out_108,
       test_video_chip_1_out_109, test_video_chip_1_out_110, test_video_chip_1_out_111,
       test_video_chip_1_out_112, test_video_chip_1_out_113, test_video_chip_1_out_114,
       test_video_chip_1_out_115, test_video_chip_1_out_116, test_video_chip_1_out_117,
       test_video_chip_1_out_118, test_video_chip_1_out_119, test_video_chip_1_out_120,
       test_video_chip_1_out_121, test_video_chip_1_out_122, test_video_chip_1_out_123,
       test_video_chip_1_out_124, test_video_chip_1_out_125, test_video_chip_1_out_126,
       test_video_chip_1_out_127, test_video_chip_1_out_128, test_video_chip_1_out_129,
       test_video_chip_1_out_130, test_video_chip_1_out_131, test_video_chip_1_out_132,
       test_video_chip_1_out_133, test_video_chip_1_out_134;

  Keyboard #(.buflen(1)) keyboard_1 (
    .re(intel_core_pentium_1_out_17), .clr(intel_core_pentium_1_out_18), .avail(keyboard_1_avail),
    .data(keyboard_1_data));  // open: clk
  Button button_1 (.out(button_1_out));
  intel_core_pentium intel_core_pentium_1 (
    .index(intel_core_pentium_1_index), .data(intel_core_pentium_1_data),
    .loaded(intel_core_pentium_1_loaded), .clock(intel_core_pentium_1_clock),
    .pacman(intel_core_pentium_1_pacman), .out_17(intel_core_pentium_1_out_17),
    .out_18(intel_core_pentium_1_out_18), .in_2(keyboard_1_avail), .all_entities(keyboard_1_data),
    .in_5(test_video_chip_1_out_136), .in_8(test_video_chip_1_out_135), .in_4(test_video_chip_1_out_138),
    .in_7(test_video_chip_1_out_137), .in_3(test_video_chip_1_out_140), .in_6(test_video_chip_1_out_139),
    .out_20(intel_core_pentium_1_out_20), .out_19(intel_core_pentium_1_out_19), .reset(button_1_out),
    .out_16(intel_core_pentium_1_out_16), .draw(intel_core_pentium_1_draw));
  DotMatrix #(.inputtype("row"), .matrixcols(30), .matrixrows(30)) dotmatrix_1 (
    .row0(test_video_chip_1_out_11), .row1(test_video_chip_1_out_13), .row2(test_video_chip_1_out_15),
    .row3(test_video_chip_1_out_17), .row4(test_video_chip_1_out_20), .row5(test_video_chip_1_out_22),
    .row6(test_video_chip_1_out_25), .row7(test_video_chip_1_out_27), .row8(test_video_chip_1_out_30),
    .row9(test_video_chip_1_out_32), .row10(test_video_chip_1_out_35), .row11(test_video_chip_1_out_37),
    .row12(test_video_chip_1_out_40), .row13(test_video_chip_1_out_42), .row14(test_video_chip_1_out_44),
    .row15(test_video_chip_1_out_46), .row16(test_video_chip_1_out_48), .row17(test_video_chip_1_out_50),
    .row18(test_video_chip_1_out_52), .row19(test_video_chip_1_out_54), .row20(test_video_chip_1_out_56),
    .row21(test_video_chip_1_out_58), .row22(test_video_chip_1_out_60), .row23(test_video_chip_1_out_62),
    .row24(test_video_chip_1_out_64), .row25(test_video_chip_1_out_66), .row26(test_video_chip_1_out_68),
    .row27(test_video_chip_1_out_70), .row28(test_video_chip_1_out_72), .row29(test_video_chip_1_out_74));
  test_video_chip test_video_chip_1 (
    .xy(intel_core_pentium_1_index), .data(intel_core_pentium_1_data), .clk(intel_core_pentium_1_clock),
    .out_10(test_video_chip_1_out_10), .out_11(test_video_chip_1_out_11), .out_12(test_video_chip_1_out_12),
    .out_13(test_video_chip_1_out_13), .out_14(test_video_chip_1_out_14), .out_15(test_video_chip_1_out_15),
    .out_16(test_video_chip_1_out_16), .out_17(test_video_chip_1_out_17), .out_19(test_video_chip_1_out_19),
    .out_20(test_video_chip_1_out_20), .out_21(test_video_chip_1_out_21), .out_22(test_video_chip_1_out_22),
    .out_24(test_video_chip_1_out_24), .out_25(test_video_chip_1_out_25), .out_26(test_video_chip_1_out_26),
    .out_27(test_video_chip_1_out_27), .out_29(test_video_chip_1_out_29), .out_30(test_video_chip_1_out_30),
    .out_31(test_video_chip_1_out_31), .out_32(test_video_chip_1_out_32), .out_34(test_video_chip_1_out_34),
    .out_35(test_video_chip_1_out_35), .out_36(test_video_chip_1_out_36), .out_37(test_video_chip_1_out_37),
    .out_39(test_video_chip_1_out_39), .out_40(test_video_chip_1_out_40), .out_41(test_video_chip_1_out_41),
    .out_42(test_video_chip_1_out_42), .out_43(test_video_chip_1_out_43), .out_44(test_video_chip_1_out_44),
    .out_45(test_video_chip_1_out_45), .out_46(test_video_chip_1_out_46), .out_47(test_video_chip_1_out_47),
    .out_48(test_video_chip_1_out_48), .out_49(test_video_chip_1_out_49), .out_50(test_video_chip_1_out_50),
    .out_51(test_video_chip_1_out_51), .out_52(test_video_chip_1_out_52), .out_53(test_video_chip_1_out_53),
    .out_54(test_video_chip_1_out_54), .out_55(test_video_chip_1_out_55), .out_56(test_video_chip_1_out_56),
    .out_57(test_video_chip_1_out_57), .out_58(test_video_chip_1_out_58), .out_59(test_video_chip_1_out_59),
    .out_60(test_video_chip_1_out_60), .out_61(test_video_chip_1_out_61), .out_62(test_video_chip_1_out_62),
    .out_63(test_video_chip_1_out_63), .out_64(test_video_chip_1_out_64), .out_65(test_video_chip_1_out_65),
    .out_66(test_video_chip_1_out_66), .out_67(test_video_chip_1_out_67), .out_68(test_video_chip_1_out_68),
    .out_69(test_video_chip_1_out_69), .out_70(test_video_chip_1_out_70), .out_71(test_video_chip_1_out_71),
    .out_72(test_video_chip_1_out_72), .out_73(test_video_chip_1_out_73), .out_74(test_video_chip_1_out_74),
    .out_75(test_video_chip_1_out_75), .out_76(test_video_chip_1_out_76), .out_77(test_video_chip_1_out_77),
    .out_78(test_video_chip_1_out_78), .out_79(test_video_chip_1_out_79), .out_80(test_video_chip_1_out_80),
    .out_81(test_video_chip_1_out_81), .out_82(test_video_chip_1_out_82), .out_83(test_video_chip_1_out_83),
    .out_84(test_video_chip_1_out_84), .out_85(test_video_chip_1_out_85), .out_86(test_video_chip_1_out_86),
    .out_87(test_video_chip_1_out_87), .out_88(test_video_chip_1_out_88), .out_89(test_video_chip_1_out_89),
    .out_90(test_video_chip_1_out_90), .out_91(test_video_chip_1_out_91), .out_92(test_video_chip_1_out_92),
    .out_93(test_video_chip_1_out_93), .out_94(test_video_chip_1_out_94), .out_95(test_video_chip_1_out_95),
    .out_96(test_video_chip_1_out_96), .out_97(test_video_chip_1_out_97), .out_98(test_video_chip_1_out_98),
    .out_99(test_video_chip_1_out_99), .out_100(test_video_chip_1_out_100),
    .out_101(test_video_chip_1_out_101), .out_102(test_video_chip_1_out_102),
    .out_103(test_video_chip_1_out_103), .out_104(test_video_chip_1_out_104),
    .out_105(test_video_chip_1_out_105), .out_106(test_video_chip_1_out_106),
    .out_107(test_video_chip_1_out_107), .out_108(test_video_chip_1_out_108),
    .out_109(test_video_chip_1_out_109), .out_110(test_video_chip_1_out_110),
    .out_111(test_video_chip_1_out_111), .out_112(test_video_chip_1_out_112),
    .out_113(test_video_chip_1_out_113), .out_114(test_video_chip_1_out_114),
    .out_115(test_video_chip_1_out_115), .out_116(test_video_chip_1_out_116),
    .out_117(test_video_chip_1_out_117), .out_118(test_video_chip_1_out_118),
    .out_119(test_video_chip_1_out_119), .out_120(test_video_chip_1_out_120),
    .out_121(test_video_chip_1_out_121), .out_122(test_video_chip_1_out_122),
    .out_123(test_video_chip_1_out_123), .out_124(test_video_chip_1_out_124),
    .out_125(test_video_chip_1_out_125), .out_126(test_video_chip_1_out_126),
    .out_127(test_video_chip_1_out_127), .out_128(test_video_chip_1_out_128),
    .out_129(test_video_chip_1_out_129), .out_130(test_video_chip_1_out_130),
    .out_131(test_video_chip_1_out_131), .out_132(test_video_chip_1_out_132),
    .out_133(test_video_chip_1_out_133), .out_134(test_video_chip_1_out_134),
    .ghost(intel_core_pentium_1_loaded), .pacman(intel_core_pentium_1_pacman),
    .draw(intel_core_pentium_1_draw), .out_135(test_video_chip_1_out_135),
    .out_136(test_video_chip_1_out_136), .out_137(test_video_chip_1_out_137),
    .out_138(test_video_chip_1_out_138), .out_139(test_video_chip_1_out_139),
    .out_140(test_video_chip_1_out_140), .win(intel_core_pentium_1_out_20),
    .lose(intel_core_pentium_1_out_19), .out_18(test_video_chip_1_out_18), .out_23(test_video_chip_1_out_23),
    .out_28(test_video_chip_1_out_28), .out_33(test_video_chip_1_out_33), .out_38(test_video_chip_1_out_38),
    .reset(intel_core_pentium_1_out_16));
  DotMatrix #(.inputtype("row"), .matrixcols(30), .matrixrows(30)) dotmatrix_2 (
    .row0(test_video_chip_1_out_76), .row1(test_video_chip_1_out_78), .row2(test_video_chip_1_out_80),
    .row3(test_video_chip_1_out_82), .row4(test_video_chip_1_out_84), .row5(test_video_chip_1_out_86),
    .row6(test_video_chip_1_out_88), .row7(test_video_chip_1_out_90), .row8(test_video_chip_1_out_92),
    .row9(test_video_chip_1_out_94), .row10(test_video_chip_1_out_96), .row11(test_video_chip_1_out_98),
    .row12(test_video_chip_1_out_100), .row13(test_video_chip_1_out_102), .row14(test_video_chip_1_out_104),
    .row15(test_video_chip_1_out_106), .row16(test_video_chip_1_out_108), .row17(test_video_chip_1_out_110),
    .row18(test_video_chip_1_out_112), .row19(test_video_chip_1_out_114), .row20(test_video_chip_1_out_116),
    .row21(test_video_chip_1_out_118), .row22(test_video_chip_1_out_120), .row23(test_video_chip_1_out_122),
    .row24(test_video_chip_1_out_124), .row25(test_video_chip_1_out_126), .row26(test_video_chip_1_out_128),
    .row27(test_video_chip_1_out_130), .row28(test_video_chip_1_out_132), .row29(test_video_chip_1_out_134));
  DotMatrix #(.inputtype("row"), .matrixcols(30), .matrixrows(5)) dotmatrix_3 (
    .row0(test_video_chip_1_out_18), .row1(test_video_chip_1_out_23), .row2(test_video_chip_1_out_28),
    .row3(test_video_chip_1_out_33), .row4(test_video_chip_1_out_38));
  DotMatrix #(.inputtype("row"), .matrixcols(30), .matrixrows(30)) dotmatrix_4 (
    .row0(test_video_chip_1_out_10), .row1(test_video_chip_1_out_12), .row2(test_video_chip_1_out_14),
    .row3(test_video_chip_1_out_16), .row4(test_video_chip_1_out_19), .row5(test_video_chip_1_out_21),
    .row6(test_video_chip_1_out_24), .row7(test_video_chip_1_out_26), .row8(test_video_chip_1_out_29),
    .row9(test_video_chip_1_out_31), .row10(test_video_chip_1_out_34), .row11(test_video_chip_1_out_36),
    .row12(test_video_chip_1_out_39), .row13(test_video_chip_1_out_41), .row14(test_video_chip_1_out_43),
    .row15(test_video_chip_1_out_45), .row16(test_video_chip_1_out_47), .row17(test_video_chip_1_out_49),
    .row18(test_video_chip_1_out_51), .row19(test_video_chip_1_out_53), .row20(test_video_chip_1_out_55),
    .row21(test_video_chip_1_out_57), .row22(test_video_chip_1_out_59), .row23(test_video_chip_1_out_61),
    .row24(test_video_chip_1_out_63), .row25(test_video_chip_1_out_65), .row26(test_video_chip_1_out_67),
    .row27(test_video_chip_1_out_69), .row28(test_video_chip_1_out_71), .row29(test_video_chip_1_out_73));
  DotMatrix #(.inputtype("row"), .matrixcols(30), .matrixrows(30)) dotmatrix_5 (
    .row0(test_video_chip_1_out_75), .row1(test_video_chip_1_out_77), .row2(test_video_chip_1_out_79),
    .row3(test_video_chip_1_out_81), .row4(test_video_chip_1_out_83), .row5(test_video_chip_1_out_85),
    .row6(test_video_chip_1_out_87), .row7(test_video_chip_1_out_89), .row8(test_video_chip_1_out_91),
    .row9(test_video_chip_1_out_93), .row10(test_video_chip_1_out_95), .row11(test_video_chip_1_out_97),
    .row12(test_video_chip_1_out_99), .row13(test_video_chip_1_out_101), .row14(test_video_chip_1_out_103),
    .row15(test_video_chip_1_out_105), .row16(test_video_chip_1_out_107), .row17(test_video_chip_1_out_109),
    .row18(test_video_chip_1_out_111), .row19(test_video_chip_1_out_113), .row20(test_video_chip_1_out_115),
    .row21(test_video_chip_1_out_117), .row22(test_video_chip_1_out_119), .row23(test_video_chip_1_out_121),
    .row24(test_video_chip_1_out_123), .row25(test_video_chip_1_out_125), .row26(test_video_chip_1_out_127),
    .row27(test_video_chip_1_out_129), .row28(test_video_chip_1_out_131), .row29(test_video_chip_1_out_133));
endmodule

module test_video_chip (
  input  clk,
  input  [8:0] xy,
  input  reset,
  input  win,
  input  lose,
  input  draw,
  input  ghost,
  input  pacman,
  input  [15:0] data,
  output [29:0] out_10,
  output [29:0] out_11,
  output [29:0] out_12,
  output [29:0] out_13,
  output [29:0] out_14,
  output [29:0] out_15,
  output [29:0] out_16,
  output [29:0] out_17,
  output [29:0] out_18,
  output [29:0] out_19,
  output [29:0] out_20,
  output [29:0] out_21,
  output [29:0] out_22,
  output [29:0] out_23,
  output [29:0] out_24,
  output [29:0] out_25,
  output [29:0] out_26,
  output [29:0] out_27,
  output [29:0] out_28,
  output [29:0] out_29,
  output [29:0] out_30,
  output [29:0] out_31,
  output [29:0] out_32,
  output [29:0] out_33,
  output [29:0] out_34,
  output [29:0] out_35,
  output [29:0] out_36,
  output [29:0] out_37,
  output [29:0] out_38,
  output [29:0] out_39,
  output [29:0] out_40,
  output [29:0] out_41,
  output [29:0] out_42,
  output [29:0] out_43,
  output [29:0] out_44,
  output [29:0] out_45,
  output [29:0] out_46,
  output [29:0] out_47,
  output [29:0] out_48,
  output [29:0] out_49,
  output [29:0] out_50,
  output [29:0] out_51,
  output [29:0] out_52,
  output [29:0] out_53,
  output [29:0] out_54,
  output [29:0] out_55,
  output [29:0] out_56,
  output [29:0] out_57,
  output [29:0] out_58,
  output [29:0] out_59,
  output [29:0] out_60,
  output [29:0] out_61,
  output [29:0] out_62,
  output [29:0] out_63,
  output [29:0] out_64,
  output [29:0] out_65,
  output [29:0] out_66,
  output [29:0] out_67,
  output [29:0] out_68,
  output [29:0] out_69,
  output [29:0] out_70,
  output [29:0] out_71,
  output [29:0] out_72,
  output [29:0] out_73,
  output [29:0] out_74,
  output [29:0] out_75,
  output [29:0] out_76,
  output [29:0] out_77,
  output [29:0] out_78,
  output [29:0] out_79,
  output [29:0] out_80,
  output [29:0] out_81,
  output [29:0] out_82,
  output [29:0] out_83,
  output [29:0] out_84,
  output [29:0] out_85,
  output [29:0] out_86,
  output [29:0] out_87,
  output [29:0] out_88,
  output [29:0] out_89,
  output [29:0] out_90,
  output [29:0] out_91,
  output [29:0] out_92,
  output [29:0] out_93,
  output [29:0] out_94,
  output [29:0] out_95,
  output [29:0] out_96,
  output [29:0] out_97,
  output [29:0] out_98,
  output [29:0] out_99,
  output [29:0] out_100,
  output [29:0] out_101,
  output [29:0] out_102,
  output [29:0] out_103,
  output [29:0] out_104,
  output [29:0] out_105,
  output [29:0] out_106,
  output [29:0] out_107,
  output [29:0] out_108,
  output [29:0] out_109,
  output [29:0] out_110,
  output [29:0] out_111,
  output [29:0] out_112,
  output [29:0] out_113,
  output [29:0] out_114,
  output [29:0] out_115,
  output [29:0] out_116,
  output [29:0] out_117,
  output [29:0] out_118,
  output [29:0] out_119,
  output [29:0] out_120,
  output [29:0] out_121,
  output [29:0] out_122,
  output [29:0] out_123,
  output [29:0] out_124,
  output [29:0] out_125,
  output [29:0] out_126,
  output [29:0] out_127,
  output [29:0] out_128,
  output [29:0] out_129,
  output [29:0] out_130,
  output [29:0] out_131,
  output [29:0] out_132,
  output [29:0] out_133,
  output [29:0] out_134,
  output [2:0] out_135,
  output [2:0] out_136,
  output [2:0] out_137,
  output [2:0] out_138,
  output [2:0] out_139,
  output [2:0] out_140
);

  wire or_6_out, transistor_1_out;
  wire [4:0] y;
  wire [8:0] divider_1_out, x;
  wire [15:0] demultiplexer_1_out16, demultiplexer_1_out17, demultiplexer_1_out18, demultiplexer_1_out19,
       pull_resistor_11_node, pull_resistor_12_node, pull_resistor_13_node, pull_resistor_14_node,
       pull_resistor_15_node, pull_resistor_16_node, pull_resistor_17_node, pull_resistor_18_node,
       pull_resistor_19_node, pull_resistor_20_node, pull_resistor_21_node, pull_resistor_22_node,
       pull_resistor_23_node, pull_resistor_24_node, pull_resistor_25_node, pull_resistor_26_node;
  wire [29:0] controlled_buffer_1_out, controlled_buffer_2_out, controlled_buffer_3_out,
       controlled_buffer_4_out, controlled_buffer_5_out, controlled_buffer_6_out, controlled_buffer_7_out,
       controlled_buffer_8_out, controlled_buffer_9_out, controlled_buffer_10_out;

  assign controlled_buffer_1_out = lose ? 30'h122071df : 30'bz;  // Controlled_Buffer controlled_buffer_1
  Pull_Resistor pull_resistor_1 (.node(controlled_buffer_1_out));
  assign out_18 = controlled_buffer_1_out | controlled_buffer_6_out;  // OR_Gate or_1, 30 bits wide
  assign controlled_buffer_2_out = lose ? 30'h12208a04 : 30'bz;  // Controlled_Buffer controlled_buffer_2
  Pull_Resistor pull_resistor_2 (.node(controlled_buffer_2_out));
  assign out_23 = controlled_buffer_2_out | controlled_buffer_7_out;  // OR_Gate or_2, 30 bits wide
  assign controlled_buffer_3_out = lose ? 30'h122089c4 : 30'bz;  // Controlled_Buffer controlled_buffer_3
  Pull_Resistor pull_resistor_3 (.node(controlled_buffer_3_out));
  assign out_28 = controlled_buffer_3_out | controlled_buffer_8_out;  // OR_Gate or_3, 30 bits wide
  assign controlled_buffer_4_out = lose ? 30'h12208824 : 30'bz;  // Controlled_Buffer controlled_buffer_4
  Pull_Resistor pull_resistor_4 (.node(controlled_buffer_4_out));
  assign out_33 = controlled_buffer_4_out | controlled_buffer_9_out;  // OR_Gate or_4, 30 bits wide
  assign controlled_buffer_5_out = lose ? 30'hc3e71c4 : 30'bz;  // Controlled_Buffer controlled_buffer_5
  Pull_Resistor pull_resistor_5 (.node(controlled_buffer_5_out));
  assign out_38 = controlled_buffer_5_out | controlled_buffer_10_out;  // OR_Gate or_5, 30 bits wide
  assign controlled_buffer_6_out = win ? 30'h9080ba1 : 30'bz;  // Controlled_Buffer controlled_buffer_6
  Pull_Resistor pull_resistor_6 (.node(controlled_buffer_6_out));
  assign controlled_buffer_7_out = win ? 30'h9088931 : 30'bz;  // Controlled_Buffer controlled_buffer_7
  Pull_Resistor pull_resistor_7 (.node(controlled_buffer_7_out));
  assign controlled_buffer_8_out = win ? 30'h9088929 : 30'bz;  // Controlled_Buffer controlled_buffer_8
  Pull_Resistor pull_resistor_8 (.node(controlled_buffer_8_out));
  assign controlled_buffer_9_out = win ? 30'h9049125 : 30'bz;  // Controlled_Buffer controlled_buffer_9
  Pull_Resistor pull_resistor_9 (.node(controlled_buffer_9_out));
  assign controlled_buffer_10_out = win ? 30'h60363a3 : 30'bz;  // Controlled_Buffer controlled_buffer_10
  Pull_Resistor pull_resistor_10 (.node(controlled_buffer_10_out));
  Pull_Resistor #(.pull(1)) pull_resistor_11 (.node(pull_resistor_11_node));
  Pull_Resistor #(.pull(1)) pull_resistor_12 (.node(pull_resistor_12_node));
  Pull_Resistor #(.pull(1)) pull_resistor_13 (.node(pull_resistor_13_node));
  Pull_Resistor #(.pull(1)) pull_resistor_14 (.node(pull_resistor_14_node));
  Pull_Resistor #(.pull(1)) pull_resistor_15 (.node(pull_resistor_15_node));
  Pull_Resistor #(.pull(1)) pull_resistor_16 (.node(pull_resistor_16_node));
  Pull_Resistor #(.pull(1)) pull_resistor_17 (.node(pull_resistor_17_node));
  Pull_Resistor #(.pull(1)) pull_resistor_18 (.node(pull_resistor_18_node));
  Pull_Resistor #(.pull(1)) pull_resistor_19 (.node(pull_resistor_19_node));
  Pull_Resistor #(.pull(1)) pull_resistor_20 (.node(pull_resistor_20_node));
  Pull_Resistor #(.pull(1)) pull_resistor_21 (.node(pull_resistor_21_node));
  Pull_Resistor #(.pull(1)) pull_resistor_22 (.node(pull_resistor_22_node));
  Pull_Resistor #(.pull(1)) pull_resistor_23 (.node(pull_resistor_23_node));
  Pull_Resistor #(.pull(1)) pull_resistor_24 (.node(pull_resistor_24_node));
  Pull_Resistor #(.pull(1)) pull_resistor_25 (.node(pull_resistor_25_node));
  Pull_Resistor #(.pull(1)) pull_resistor_26 (.node(pull_resistor_26_node));
  Demultiplexer #(.select(5), .width(16), .tristate("true"), .enable("false")) demultiplexer_1 (
    .out0(pull_resistor_11_node), .out1(pull_resistor_12_node), .out2(pull_resistor_13_node),
    .out3(pull_resistor_14_node), .out4(pull_resistor_15_node), .out5(pull_resistor_16_node),
    .out6(pull_resistor_17_node), .out7(pull_resistor_18_node), .out8(pull_resistor_19_node),
    .out9(pull_resistor_20_node), .out10(pull_resistor_21_node), .out11(pull_resistor_22_node),
    .out12(pull_resistor_23_node), .out13(pull_resistor_24_node), .out14(pull_resistor_25_node),
    .out15(pull_resistor_26_node), .out16(demultiplexer_1_out16), .out17(demultiplexer_1_out17),
    .out18(demultiplexer_1_out18), .out19(demultiplexer_1_out19), .in(data), .sel(y));  // open: out20, out21, out22, out23, out24, out25, out26, out27, out28, out29, out30, out31
  Pull_Resistor #(.pull(1)) pull_resistor_27 (.node(demultiplexer_1_out16));
  Pull_Resistor #(.pull(1)) pull_resistor_28 (.node(demultiplexer_1_out17));
  Pull_Resistor #(.pull(1)) pull_resistor_29 (.node(demultiplexer_1_out18));
  Pull_Resistor #(.pull(1)) pull_resistor_30 (.node(demultiplexer_1_out19));
  Divider #(.width(9)) divider_1 (.a(xy), .b(9'h14), .out(divider_1_out), .rem(x));  // open: upper
  Bit_Extender #(.in_width(9), .out_width(5)) bit_extender_1 (.in(divider_1_out), .out(y));
  test_row_handler test_row_handler_1 (
    .x(x), .data(pull_resistor_11_node), .clk(clk), .out_8(out_10), .out_9(out_12), .out_10(out_14),
    .out_11(out_11), .out_12(out_13), .out_13(out_15), .ghost(ghost), .pacman(pacman), .draw(draw),
    .out_14(out_135), .reset(transistor_1_out), .out_15(out_136), .out_16(out_137), .out_17(out_138),
    .out_18(out_139), .out_19(out_140));
  test_row_handler test_row_handler_2 (
    .x(x), .data(pull_resistor_12_node), .clk(clk), .out_8(out_16), .out_9(out_19), .out_10(out_21),
    .out_11(out_17), .out_12(out_20), .out_13(out_22), .ghost(ghost), .pacman(pacman), .draw(draw),
    .out_14(out_135), .reset(transistor_1_out), .out_15(out_136), .out_16(out_137), .out_17(out_138),
    .out_18(out_139), .out_19(out_140));
  test_row_handler test_row_handler_3 (
    .x(x), .data(pull_resistor_13_node), .clk(clk), .out_8(out_24), .out_9(out_26), .out_10(out_29),
    .out_11(out_25), .out_12(out_27), .out_13(out_30), .ghost(ghost), .pacman(pacman), .draw(draw),
    .out_14(out_135), .reset(transistor_1_out), .out_15(out_136), .out_16(out_137), .out_17(out_138),
    .out_18(out_139), .out_19(out_140));
  test_row_handler test_row_handler_4 (
    .x(x), .data(pull_resistor_14_node), .clk(clk), .out_8(out_31), .out_9(out_34), .out_10(out_36),
    .out_11(out_32), .out_12(out_35), .out_13(out_37), .ghost(ghost), .pacman(pacman), .draw(draw),
    .out_14(out_135), .reset(transistor_1_out), .out_15(out_136), .out_16(out_137), .out_17(out_138),
    .out_18(out_139), .out_19(out_140));
  test_row_handler test_row_handler_5 (
    .x(x), .data(pull_resistor_15_node), .clk(clk), .out_8(out_39), .out_9(out_41), .out_10(out_43),
    .out_11(out_40), .out_12(out_42), .out_13(out_44), .ghost(ghost), .pacman(pacman), .draw(draw),
    .out_14(out_135), .reset(transistor_1_out), .out_15(out_136), .out_16(out_137), .out_17(out_138),
    .out_18(out_139), .out_19(out_140));
  test_row_handler test_row_handler_6 (
    .x(x), .data(pull_resistor_16_node), .clk(clk), .out_8(out_45), .out_9(out_47), .out_10(out_49),
    .out_11(out_46), .out_12(out_48), .out_13(out_50), .ghost(ghost), .pacman(pacman), .draw(draw),
    .out_14(out_135), .reset(transistor_1_out), .out_15(out_136), .out_16(out_137), .out_17(out_138),
    .out_18(out_139), .out_19(out_140));
  test_row_handler test_row_handler_7 (
    .x(x), .data(pull_resistor_17_node), .clk(clk), .out_8(out_51), .out_9(out_53), .out_10(out_55),
    .out_11(out_52), .out_12(out_54), .out_13(out_56), .ghost(ghost), .pacman(pacman), .draw(draw),
    .out_14(out_135), .reset(transistor_1_out), .out_15(out_136), .out_16(out_137), .out_17(out_138),
    .out_18(out_139), .out_19(out_140));
  test_row_handler test_row_handler_8 (
    .x(x), .data(pull_resistor_18_node), .clk(clk), .out_8(out_57), .out_9(out_59), .out_10(out_61),
    .out_11(out_58), .out_12(out_60), .out_13(out_62), .ghost(ghost), .pacman(pacman), .draw(draw),
    .out_14(out_135), .reset(transistor_1_out), .out_15(out_136), .out_16(out_137), .out_17(out_138),
    .out_18(out_139), .out_19(out_140));
  test_row_handler test_row_handler_9 (
    .x(x), .data(pull_resistor_19_node), .clk(clk), .out_8(out_63), .out_9(out_65), .out_10(out_67),
    .out_11(out_64), .out_12(out_66), .out_13(out_68), .ghost(ghost), .pacman(pacman), .draw(draw),
    .out_14(out_135), .reset(transistor_1_out), .out_15(out_136), .out_16(out_137), .out_17(out_138),
    .out_18(out_139), .out_19(out_140));
  test_row_handler test_row_handler_10 (
    .x(x), .data(pull_resistor_20_node), .clk(clk), .out_8(out_69), .out_9(out_71), .out_10(out_73),
    .out_11(out_70), .out_12(out_72), .out_13(out_74), .ghost(ghost), .pacman(pacman), .draw(draw),
    .out_14(out_135), .reset(transistor_1_out), .out_15(out_136), .out_16(out_137), .out_17(out_138),
    .out_18(out_139), .out_19(out_140));
  test_row_handler test_row_handler_11 (
    .x(x), .data(pull_resistor_21_node), .clk(clk), .out_8(out_75), .out_9(out_77), .out_10(out_79),
    .out_11(out_76), .out_12(out_78), .out_13(out_80), .ghost(ghost), .pacman(pacman), .draw(draw),
    .out_14(out_135), .reset(transistor_1_out), .out_15(out_136), .out_16(out_137), .out_17(out_138),
    .out_18(out_139), .out_19(out_140));
  test_row_handler test_row_handler_12 (
    .x(x), .data(pull_resistor_22_node), .clk(clk), .out_8(out_81), .out_9(out_83), .out_10(out_85),
    .out_11(out_82), .out_12(out_84), .out_13(out_86), .ghost(ghost), .pacman(pacman), .draw(draw),
    .out_14(out_135), .reset(transistor_1_out), .out_15(out_136), .out_16(out_137), .out_17(out_138),
    .out_18(out_139), .out_19(out_140));
  test_row_handler test_row_handler_13 (
    .x(x), .data(pull_resistor_23_node), .clk(clk), .out_8(out_87), .out_9(out_89), .out_10(out_91),
    .out_11(out_88), .out_12(out_90), .out_13(out_92), .ghost(ghost), .pacman(pacman), .draw(draw),
    .out_14(out_135), .reset(transistor_1_out), .out_15(out_136), .out_16(out_137), .out_17(out_138),
    .out_18(out_139), .out_19(out_140));
  test_row_handler test_row_handler_14 (
    .x(x), .data(pull_resistor_24_node), .clk(clk), .out_8(out_93), .out_9(out_95), .out_10(out_97),
    .out_11(out_94), .out_12(out_96), .out_13(out_98), .ghost(ghost), .pacman(pacman), .draw(draw),
    .out_14(out_135), .reset(transistor_1_out), .out_15(out_136), .out_16(out_137), .out_17(out_138),
    .out_18(out_139), .out_19(out_140));
  test_row_handler test_row_handler_15 (
    .x(x), .data(pull_resistor_25_node), .clk(clk), .out_8(out_99), .out_9(out_101), .out_10(out_103),
    .out_11(out_100), .out_12(out_102), .out_13(out_104), .ghost(ghost), .pacman(pacman), .draw(draw),
    .out_14(out_135), .reset(transistor_1_out), .out_15(out_136), .out_16(out_137), .out_17(out_138),
    .out_18(out_139), .out_19(out_140));
  test_row_handler test_row_handler_16 (
    .x(x), .data(pull_resistor_26_node), .clk(clk), .out_8(out_105), .out_9(out_107), .out_10(out_109),
    .out_11(out_106), .out_12(out_108), .out_13(out_110), .ghost(ghost), .pacman(pacman), .draw(draw),
    .out_14(out_135), .reset(transistor_1_out), .out_15(out_136), .out_16(out_137), .out_17(out_138),
    .out_18(out_139), .out_19(out_140));
  test_row_handler test_row_handler_17 (
    .x(x), .data(demultiplexer_1_out16), .clk(clk), .out_8(out_111), .out_9(out_113), .out_10(out_115),
    .out_11(out_112), .out_12(out_114), .out_13(out_116), .ghost(ghost), .pacman(pacman), .draw(draw),
    .out_14(out_135), .reset(transistor_1_out), .out_15(out_136), .out_16(out_137), .out_17(out_138),
    .out_18(out_139), .out_19(out_140));
  test_row_handler test_row_handler_18 (
    .x(x), .data(demultiplexer_1_out17), .clk(clk), .out_8(out_117), .out_9(out_119), .out_10(out_121),
    .out_11(out_118), .out_12(out_120), .out_13(out_122), .ghost(ghost), .pacman(pacman), .draw(draw),
    .out_14(out_135), .reset(transistor_1_out), .out_15(out_136), .out_16(out_137), .out_17(out_138),
    .out_18(out_139), .out_19(out_140));
  test_row_handler test_row_handler_19 (
    .x(x), .data(demultiplexer_1_out18), .clk(clk), .out_8(out_123), .out_9(out_125), .out_10(out_127),
    .out_11(out_124), .out_12(out_126), .out_13(out_128), .ghost(ghost), .pacman(pacman), .draw(draw),
    .out_14(out_135), .reset(transistor_1_out), .out_15(out_136), .out_16(out_137), .out_17(out_138),
    .out_18(out_139), .out_19(out_140));
  test_row_handler test_row_handler_20 (
    .x(x), .data(demultiplexer_1_out19), .clk(clk), .out_8(out_129), .out_9(out_131), .out_10(out_133),
    .out_11(out_130), .out_12(out_132), .out_13(out_134), .ghost(ghost), .pacman(pacman), .draw(draw),
    .out_14(out_135), .reset(transistor_1_out), .out_15(out_136), .out_16(out_137), .out_17(out_138),
    .out_18(out_139), .out_19(out_140));
  Pull_Resistor pull_resistor_31 (.node(out_135));
  Pull_Resistor pull_resistor_32 (.node(out_136));
  or or_6 (or_6_out, win, lose);
  Pull_Resistor pull_resistor_33 (.node(out_137));
  Transistor #(.\type ("n")) transistor_1 (.in(clk), .out(transistor_1_out), .gate(or_6_out));
  Transistor transistor_2 (.in(reset), .out(transistor_1_out), .gate(or_6_out));
  Pull_Resistor pull_resistor_34 (.node(out_138));
  Pull_Resistor pull_resistor_35 (.node(out_139));
  Pull_Resistor pull_resistor_36 (.node(out_140));

  // Notes on the sheet:
  //   VIDEO CHIP
endmodule

module test_row_handler (
  input  pacman,
  input  ghost,
  input  [8:0] x,
  input  [15:0] data,
  input  clk,
  input  draw,
  input  reset,
  output [29:0] out_8,
  output [29:0] out_9,
  output [29:0] out_10,
  output [29:0] out_11,
  output [29:0] out_12,
  output [29:0] out_13,
  output [2:0] out_14,
  output [2:0] out_15,
  output [2:0] out_16,
  output [2:0] out_17,
  output [2:0] out_18,
  output [2:0] out_19
);

  wire comparator_1_eq, comparator_2_eq, comparator_3_eq, comparator_4_eq, comparator_5_eq, comparator_6_eq,
       comparator_7_eq, controlled_buffer_5_out, controlled_buffer_22_out, controlled_buffer_23_out,
       not_1_out, not_2_out, not_3_out, not_4_out, not_5_out, not_6_out, not_7_out, not_8_out, not_9_out,
       not_10_out, not_11_out, not_12_out, not_13_out, or_13_out, transistor_2_out;
  wire [2:0] sprite_dict_1_out_2, sprite_dict_1_out_3, sprite_dict_1_out_4, sprite_dict_2_out_2,
       sprite_dict_2_out_3, sprite_dict_2_out_4;
  wire [4:0] bit_extender_1_out, bit_extender_2_out, bit_extender_4_out, divider_1_out, divider_1_rem, x_t;
  wire [15:0] transistor_1_out;
  wire [29:0] bit_extender_6_out, bit_extender_7_out, bit_extender_8_out, bit_extender_9_out,
       bit_extender_10_out, bit_extender_11_out, controlled_buffer_1_out, controlled_buffer_2_out,
       controlled_buffer_3_out, controlled_buffer_4_out, controlled_buffer_6_out, controlled_buffer_7_out,
       controlled_buffer_8_out, controlled_buffer_9_out, controlled_buffer_11_out, controlled_buffer_13_out,
       controlled_buffer_14_out, controlled_buffer_15_out, controlled_buffer_16_out,
       controlled_buffer_17_out, controlled_buffer_18_out, controlled_buffer_19_out,
       controlled_buffer_20_out, controlled_buffer_21_out, controlled_buffer_24_out,
       controlled_buffer_25_out, controlled_buffer_26_out, controlled_buffer_28_out,
       controlled_buffer_29_out, controlled_buffer_30_out, controlled_buffer_31_out,
       controlled_buffer_32_out, or_1_out, or_2_out, or_3_out, or_4_out, or_5_out, or_6_out, or_7_out,
       or_8_out, or_9_out, or_10_out, or_11_out, or_12_out, pull_resistor_2_node, pull_resistor_3_node,
       pull_resistor_16_node, reg1, reg2, reg3, reg4, reg5, reg6, register_7_q, register_8_q, register_9_q,
       register_10_q, register_11_q, register_12_q, rg1, rg2, rg3, rg4, rg5, rg6, shifter_1_out,
       shifter_2_out, shifter_3_out, shifter_4_out, shifter_5_out, shifter_6_out, shifter_7_out,
       shifter_8_out, shifter_9_out, shifter_10_out, shifter_11_out, shifter_12_out, xor_1_out, xor_2_out,
       xor_3_out, xor_4_out, xor_5_out, xor_6_out;

  Comparator #(.width(16), .mode("unsigned")) comparator_1 (
    .a(data), .b({16{1'b1}}), .eq(comparator_1_eq));  // open: gt, lt
  Shifter #(.width(30), .shift("lr")) shifter_1 (.in(controlled_buffer_1_out), .\dist (x_t), .out(shifter_1_out));
  assign controlled_buffer_1_out = not_1_out ? controlled_buffer_2_out : 30'bz;  // Controlled_Buffer controlled_buffer_1
  not not_1 (not_1_out, comparator_1_eq);
  assign controlled_buffer_2_out = not_2_out ? rg6 : 30'bz;  // Controlled_Buffer controlled_buffer_2
  not not_2 (not_2_out, comparator_2_eq);
  Comparator #(.width(30)) comparator_2 (.a(rg6), .b({30{1'b0}}), .eq(comparator_2_eq));  // open: gt, lt
  Bit_Extender #(.in_width(16), .out_width(5)) bit_extender_1 (.in(transistor_1_out), .out(bit_extender_1_out));
  Transistor #(.gate("br"), .width(16)) transistor_1 (.in(data), .out(transistor_1_out), .gate(comparator_1_eq));
  Bit_Extender #(.in_width(16), .out_width(5)) bit_extender_2 (.in(transistor_1_out), .out(bit_extender_2_out));
  not not_3 (not_3_out, comparator_1_eq);
  Transistor transistor_2 (.in(clk), .out(transistor_2_out), .gate(comparator_1_eq));
  Bit_Extender #(.in_width(30), .out_width(3)) bit_extender_3 (.in(shifter_1_out), .out(out_14));
  Bit_Extender #(.in_width(9), .out_width(5)) bit_extender_4 (.in(x), .out(bit_extender_4_out));
  sprite_dict sprite_dict_1 (
    .in_1(bit_extender_1_out), .out_2(sprite_dict_1_out_2), .out_3(sprite_dict_1_out_3),
    .out_4(sprite_dict_1_out_4));
  sprite_dict sprite_dict_2 (
    .in_1(bit_extender_2_out), .out_2(sprite_dict_2_out_2), .out_3(sprite_dict_2_out_3),
    .out_4(sprite_dict_2_out_4));
  assign controlled_buffer_3_out = not_1_out ? controlled_buffer_4_out : 30'bz;  // Controlled_Buffer controlled_buffer_3
  assign controlled_buffer_4_out = not_4_out ? rg5 : 30'bz;  // Controlled_Buffer controlled_buffer_4
  not not_4 (not_4_out, comparator_3_eq);
  not not_5 (not_5_out, divider_1_out[0]);
  Divider #(.width(5)) divider_1 (
    .a(bit_extender_4_out), .b(5'b01010), .out(divider_1_out), .rem(divider_1_rem));  // open: upper
  Multiplier #(.width(5)) multiplier_1 (.a(divider_1_rem), .b(5'b00011), .out(x_t));  // open: cin, cout
  Shifter #(.width(30), .shift("lr")) shifter_2 (.in(controlled_buffer_3_out), .\dist (x_t), .out(shifter_2_out));
  Bit_Extender #(.in_width(30), .out_width(3)) bit_extender_5 (.in(shifter_2_out), .out(out_15));
  Comparator #(.width(30)) comparator_3 (.a(rg5), .b({30{1'b0}}), .eq(comparator_3_eq));  // open: gt, lt
  assign controlled_buffer_5_out = not_9_out ? ghost : 1'bz;  // Controlled_Buffer controlled_buffer_5
  Pull_Resistor pull_resistor_1 (.node(controlled_buffer_5_out));
  not not_6 (not_6_out, controlled_buffer_5_out);
  assign bit_extender_6_out = {{27{1'b0}}, {sprite_dict_1_out_2[0], sprite_dict_1_out_2[1], sprite_dict_1_out_2[2]}};  // Bit_Extender bit_extender_6
  not not_7 (not_7_out, not_5_out);
  assign bit_extender_7_out = {{27{1'b0}}, {sprite_dict_1_out_3[0], sprite_dict_1_out_3[1], sprite_dict_1_out_3[2]}};  // Bit_Extender bit_extender_7
  assign bit_extender_8_out = {{27{1'b0}}, {sprite_dict_1_out_4[0], sprite_dict_1_out_4[1], sprite_dict_1_out_4[2]}};  // Bit_Extender bit_extender_8
  assign bit_extender_9_out = {{27{1'b0}}, {sprite_dict_2_out_2[0], sprite_dict_2_out_2[1], sprite_dict_2_out_2[2]}};  // Bit_Extender bit_extender_9
  assign bit_extender_10_out = {{27{1'b0}}, {sprite_dict_2_out_3[0], sprite_dict_2_out_3[1], sprite_dict_2_out_3[2]}};  // Bit_Extender bit_extender_10
  assign bit_extender_11_out = {{27{1'b0}}, {sprite_dict_2_out_4[0], sprite_dict_2_out_4[1], sprite_dict_2_out_4[2]}};  // Bit_Extender bit_extender_11
  assign controlled_buffer_6_out = not_1_out ? controlled_buffer_7_out : 30'bz;  // Controlled_Buffer controlled_buffer_6
  assign controlled_buffer_7_out = not_8_out ? rg4 : 30'bz;  // Controlled_Buffer controlled_buffer_7
  not not_8 (not_8_out, comparator_4_eq);
  not not_9 (not_9_out, pacman);
  assign controlled_buffer_8_out = not_5_out ? shifter_3_out : 30'bz;  // Controlled_Buffer controlled_buffer_8
  Shifter #(.width(30)) shifter_3 (.in(bit_extender_6_out), .\dist (x_t), .out(shifter_3_out));
  Shifter #(.width(30)) shifter_4 (.in(bit_extender_7_out), .\dist (x_t), .out(shifter_4_out));
  Shifter #(.width(30)) shifter_5 (.in(bit_extender_8_out), .\dist (x_t), .out(shifter_5_out));
  Shifter #(.width(30)) shifter_6 (.in(bit_extender_9_out), .\dist (x_t), .out(shifter_6_out));
  assign controlled_buffer_9_out = not_7_out ? shifter_6_out : 30'bz;  // Controlled_Buffer controlled_buffer_9
  Shifter #(.width(30)) shifter_7 (.in(bit_extender_10_out), .\dist (x_t), .out(shifter_7_out));
  Shifter #(.width(30)) shifter_8 (.in(bit_extender_11_out), .\dist (x_t), .out(shifter_8_out));
  Shifter #(.width(30), .shift("lr")) shifter_9 (.in(controlled_buffer_6_out), .\dist (x_t), .out(shifter_9_out));
  Comparator #(.width(30)) comparator_4 (.a(rg4), .b({30{1'b0}}), .eq(comparator_4_eq));  // open: gt, lt
  not not_10 (not_10_out, pacman);
  Pull_Resistor pull_resistor_2 (.node(pull_resistor_2_node));
  assign pull_resistor_2_node = not_10_out ? shifter_3_out : 30'bz;  // Controlled_Buffer controlled_buffer_10
  assign controlled_buffer_11_out = not_5_out ? shifter_4_out : 30'bz;  // Controlled_Buffer controlled_buffer_11
  Pull_Resistor pull_resistor_3 (.node(pull_resistor_3_node));
  assign pull_resistor_3_node = not_10_out ? shifter_4_out : 30'bz;  // Controlled_Buffer controlled_buffer_12
  assign controlled_buffer_13_out = not_5_out ? shifter_5_out : 30'bz;  // Controlled_Buffer controlled_buffer_13
  assign controlled_buffer_14_out = not_10_out ? shifter_5_out : 30'bz;  // Controlled_Buffer controlled_buffer_14
  Pull_Resistor pull_resistor_4 (.node(controlled_buffer_14_out));
  assign controlled_buffer_15_out = not_10_out ? shifter_6_out : 30'bz;  // Controlled_Buffer controlled_buffer_15
  assign controlled_buffer_16_out = not_10_out ? shifter_7_out : 30'bz;  // Controlled_Buffer controlled_buffer_16
  assign controlled_buffer_17_out = not_7_out ? shifter_7_out : 30'bz;  // Controlled_Buffer controlled_buffer_17
  assign controlled_buffer_18_out = not_10_out ? shifter_8_out : 30'bz;  // Controlled_Buffer controlled_buffer_18
  assign controlled_buffer_19_out = not_7_out ? shifter_8_out : 30'bz;  // Controlled_Buffer controlled_buffer_19
  Bit_Extender #(.in_width(30), .out_width(3)) bit_extender_12 (.in(shifter_9_out), .out(out_16));
  Pull_Resistor pull_resistor_5 (.node(controlled_buffer_15_out));
  Pull_Resistor pull_resistor_6 (.node(controlled_buffer_16_out));
  Pull_Resistor pull_resistor_7 (.node(controlled_buffer_18_out));
  Shifter #(.width(30), .shift("lr")) shifter_10 (.in(controlled_buffer_20_out), .\dist (x_t), .out(shifter_10_out));
  assign controlled_buffer_20_out = not_1_out ? controlled_buffer_21_out : 30'bz;  // Controlled_Buffer controlled_buffer_20
  assign controlled_buffer_21_out = not_11_out ? rg3 : 30'bz;  // Controlled_Buffer controlled_buffer_21
  not not_11 (not_11_out, comparator_5_eq);
  Comparator #(.width(30)) comparator_5 (.a(rg3), .b({30{1'b0}}), .eq(comparator_5_eq));  // open: gt, lt
  assign or_1_out = reg1 | pull_resistor_2_node;  // OR_Gate or_1, 30 bits wide
  assign xor_1_out = or_1_out ^ rg1;  // XOR_Gate xor_1, 30 bits wide
  assign or_2_out = reg2 | pull_resistor_3_node;  // OR_Gate or_2, 30 bits wide
  assign xor_2_out = or_2_out ^ rg2;  // XOR_Gate xor_2, 30 bits wide
  assign or_3_out = reg3 | controlled_buffer_14_out;  // OR_Gate or_3, 30 bits wide
  assign xor_3_out = or_3_out ^ rg3;  // XOR_Gate xor_3, 30 bits wide
  assign or_4_out = reg4 | controlled_buffer_15_out;  // OR_Gate or_4, 30 bits wide
  assign xor_4_out = or_4_out ^ rg4;  // XOR_Gate xor_4, 30 bits wide
  assign or_5_out = reg5 | controlled_buffer_16_out;  // OR_Gate or_5, 30 bits wide
  assign xor_5_out = or_5_out ^ rg5;  // XOR_Gate xor_5, 30 bits wide
  assign or_6_out = reg6 | controlled_buffer_18_out;  // OR_Gate or_6, 30 bits wide
  assign xor_6_out = or_6_out ^ rg6;  // XOR_Gate xor_6, 30 bits wide
  Bit_Extender #(.in_width(30), .out_width(3)) bit_extender_13 (.in(shifter_10_out), .out(out_17));
  assign controlled_buffer_22_out = not_6_out ? not_5_out : 1'bz;  // Controlled_Buffer controlled_buffer_22
  Pull_Resistor pull_resistor_8 (.node(controlled_buffer_22_out));
  Register #(.width(30)) register_1 (
    .D(xor_1_out), .en(controlled_buffer_22_out), .Q(reg1), .clk(transistor_2_out), .clr(reset));
  Register #(.width(30)) register_2 (
    .D(xor_2_out), .en(controlled_buffer_22_out), .Q(reg2), .clk(transistor_2_out), .clr(reset));
  Register #(.width(30)) register_3 (
    .D(xor_3_out), .en(controlled_buffer_22_out), .Q(reg3), .clk(transistor_2_out), .clr(reset));
  assign controlled_buffer_23_out = not_6_out ? not_7_out : 1'bz;  // Controlled_Buffer controlled_buffer_23
  Pull_Resistor pull_resistor_9 (.node(controlled_buffer_23_out));
  Register #(.width(30)) register_4 (
    .D(xor_4_out), .en(controlled_buffer_23_out), .Q(reg4), .clk(transistor_2_out), .clr(reset));
  Register #(.width(30)) register_5 (
    .D(xor_5_out), .en(controlled_buffer_23_out), .Q(reg5), .clk(transistor_2_out), .clr(reset));
  Register #(.width(30)) register_6 (
    .D(xor_6_out), .en(controlled_buffer_23_out), .Q(reg6), .clk(transistor_2_out), .clr(reset));
  assign controlled_buffer_24_out = not_1_out ? controlled_buffer_25_out : 30'bz;  // Controlled_Buffer controlled_buffer_24
  assign controlled_buffer_25_out = not_12_out ? rg2 : 30'bz;  // Controlled_Buffer controlled_buffer_25
  not not_12 (not_12_out, comparator_6_eq);
  Pull_Resistor pull_resistor_10 (.node(controlled_buffer_8_out));
  Pull_Resistor pull_resistor_11 (.node(controlled_buffer_11_out));
  Pull_Resistor pull_resistor_12 (.node(controlled_buffer_13_out));
  Pull_Resistor pull_resistor_13 (.node(controlled_buffer_9_out));
  Pull_Resistor pull_resistor_14 (.node(controlled_buffer_17_out));
  Shifter #(.width(30), .shift("lr")) shifter_11 (.in(controlled_buffer_24_out), .\dist (x_t), .out(shifter_11_out));
  Bit_Extender #(.in_width(30), .out_width(3)) bit_extender_14 (.in(shifter_11_out), .out(out_18));
  Comparator #(.width(30)) comparator_6 (.a(rg2), .b({30{1'b0}}), .eq(comparator_6_eq));  // open: gt, lt
  get_sprite_from_row get_sprite_from_row_1 (
    .in_2(reg1), .in_3(reg2), .in_4(reg3), .in_5(bit_extender_4_out), .in_6(reg4), .in_7(reg5), .in_8(reg6),
    .out_10(rg2), .out_9(rg1), .out_11(rg3), .out_12(rg4), .out_13(rg5), .out_14(rg6), .in_1(pacman));
  assign controlled_buffer_26_out = not_3_out ? controlled_buffer_8_out : 30'bz;  // Controlled_Buffer controlled_buffer_26
  Pull_Resistor pull_resistor_15 (.node(controlled_buffer_26_out));
  Pull_Resistor pull_resistor_16 (.node(pull_resistor_16_node));
  assign pull_resistor_16_node = not_3_out ? controlled_buffer_11_out : 30'bz;  // Controlled_Buffer controlled_buffer_27
  assign controlled_buffer_28_out = not_3_out ? controlled_buffer_13_out : 30'bz;  // Controlled_Buffer controlled_buffer_28
  Pull_Resistor pull_resistor_17 (.node(controlled_buffer_28_out));
  assign controlled_buffer_29_out = not_3_out ? controlled_buffer_9_out : 30'bz;  // Controlled_Buffer controlled_buffer_29
  Pull_Resistor pull_resistor_18 (.node(controlled_buffer_29_out));
  assign controlled_buffer_30_out = not_3_out ? controlled_buffer_17_out : 30'bz;  // Controlled_Buffer controlled_buffer_30
  Pull_Resistor pull_resistor_19 (.node(controlled_buffer_30_out));
  assign controlled_buffer_31_out = not_3_out ? controlled_buffer_19_out : 30'bz;  // Controlled_Buffer controlled_buffer_31
  Pull_Resistor pull_resistor_20 (.node(controlled_buffer_31_out));
  Pull_Resistor pull_resistor_21 (.node(controlled_buffer_19_out));
  Controlled_Buffer #(.width(30)) controlled_buffer_32 (.out(controlled_buffer_32_out), .en(not_1_out));  // open: in
  Controlled_Buffer #(.width(30)) controlled_buffer_33 (.in(rg1), .en(not_13_out));  // open: out
  not not_13 (not_13_out, comparator_7_eq);
  assign or_7_out = reg1 | register_7_q | controlled_buffer_26_out;  // OR_Gate or_7, 30 bits wide
  assign or_8_out = pull_resistor_16_node | register_8_q | reg2;  // OR_Gate or_8, 30 bits wide
  assign or_9_out = controlled_buffer_28_out | register_9_q | reg3;  // OR_Gate or_9, 30 bits wide
  assign or_10_out = reg4 | register_10_q | controlled_buffer_29_out;  // OR_Gate or_10, 30 bits wide
  assign or_11_out = reg5 | register_11_q | controlled_buffer_30_out;  // OR_Gate or_11, 30 bits wide
  assign or_12_out = controlled_buffer_31_out | register_12_q | reg6;  // OR_Gate or_12, 30 bits wide
  Shifter #(.width(30), .shift("lr")) shifter_12 (.in(controlled_buffer_32_out), .\dist (x_t), .out(shifter_12_out));
  Comparator #(.width(30)) comparator_7 (.a(rg1), .b({30{1'b0}}), .eq(comparator_7_eq));  // open: gt, lt
  Register #(.width(30)) register_7 (.D(or_7_out), .Q(register_7_q), .clk(clk), .clr(or_13_out));  // open: en
  Register #(.width(30)) register_8 (.D(or_8_out), .Q(register_8_q), .clk(clk), .clr(or_13_out));  // open: en
  Register #(.width(30)) register_9 (.D(or_9_out), .Q(register_9_q), .clk(clk), .clr(or_13_out));  // open: en
  Register #(.width(30)) register_10 (.D(or_10_out), .Q(register_10_q), .clk(clk), .clr(or_13_out));  // open: en
  Register #(.width(30)) register_11 (.D(or_11_out), .Q(register_11_q), .clk(clk), .clr(or_13_out));  // open: en
  Register #(.width(30)) register_12 (.D(or_12_out), .Q(register_12_q), .clk(clk), .clr(or_13_out));  // open: en
  or or_13 (or_13_out, draw, reset);
  Bit_Extender #(.in_width(30), .out_width(3)) bit_extender_15 (.in(shifter_12_out), .out(out_19));
  Register #(.width(30)) register_13 (.D(register_7_q), .Q(out_8), .clk(or_13_out), .clr(reset));  // open: en
  Register #(.width(30)) register_14 (.D(register_8_q), .Q(out_9), .clk(or_13_out), .clr(reset));  // open: en
  Register #(.width(30)) register_15 (.D(register_9_q), .Q(out_10), .clk(or_13_out), .clr(reset));  // open: en
  Register #(.width(30)) register_16 (.D(register_10_q), .Q(out_11), .clk(or_13_out), .clr(reset));  // open: en
  Register #(.width(30)) register_17 (.D(register_11_q), .Q(out_12), .clk(or_13_out), .clr(reset));  // open: en
  Register #(.width(30)) register_18 (.D(register_12_q), .Q(out_13), .clk(or_13_out), .clr(reset));  // open: en

  // Notes on the sheet:
  //   ROW HANDLER
endmodule

module get_sprite_from_row (
  input  in_1,
  input  [29:0] in_2,
  input  [29:0] in_3,
  input  [29:0] in_4,
  input  [4:0] in_5,
  input  [29:0] in_6,
  input  [29:0] in_7,
  input  [29:0] in_8,
  output [29:0] out_9,
  output [29:0] out_10,
  output [29:0] out_11,
  output [29:0] out_12,
  output [29:0] out_13,
  output [29:0] out_14
);

  wire not_1_out;
  wire [4:0] divider_1_out, divider_1_rem;
  wire [29:0] controlled_buffer_1_out, controlled_buffer_2_out, get_next_sprite_1_out_5,
       get_next_sprite_1_out_6, get_next_sprite_1_out_7, get_next_sprite_2_out_5, get_next_sprite_2_out_6,
       get_next_sprite_2_out_7, pull_resistor_3_node, pull_resistor_4_node, pull_resistor_5_node,
       pull_resistor_6_node;

  // Probe on in_5
  Divider #(.width(5)) divider_1 (.a(in_5), .b(5'b01010), .out(divider_1_out), .rem(divider_1_rem));  // open: upper
  get_next_sprite get_next_sprite_1 (
    .sprite_reg(in_2), .sprite_reg_2(in_3), .sprite_reg_3(in_4), .x(divider_1_rem),
    .out_5(get_next_sprite_1_out_5), .out_6(get_next_sprite_1_out_6), .out_7(get_next_sprite_1_out_7));
  not not_1 (not_1_out, divider_1_out[0]);
  get_next_sprite get_next_sprite_2 (
    .sprite_reg(in_6), .sprite_reg_2(in_7), .sprite_reg_3(in_8), .x(divider_1_rem),
    .out_5(get_next_sprite_2_out_5), .out_6(get_next_sprite_2_out_6), .out_7(get_next_sprite_2_out_7));
  assign controlled_buffer_1_out = not_1_out ? get_next_sprite_1_out_5 : 30'bz;  // Controlled_Buffer controlled_buffer_1
  Pull_Resistor pull_resistor_1 (.node(controlled_buffer_1_out));
  assign controlled_buffer_2_out = not_1_out ? get_next_sprite_1_out_6 : 30'bz;  // Controlled_Buffer controlled_buffer_2
  Pull_Resistor pull_resistor_2 (.node(controlled_buffer_2_out));
  Pull_Resistor pull_resistor_3 (.node(pull_resistor_3_node));
  assign pull_resistor_3_node = not_1_out ? get_next_sprite_1_out_7 : 30'bz;  // Controlled_Buffer controlled_buffer_3
  Pull_Resistor pull_resistor_4 (.node(pull_resistor_4_node));
  assign pull_resistor_4_node = divider_1_out[0] ? get_next_sprite_2_out_5 : 30'bz;  // Controlled_Buffer controlled_buffer_4
  Pull_Resistor pull_resistor_5 (.node(pull_resistor_5_node));
  assign pull_resistor_5_node = divider_1_out[0] ? get_next_sprite_2_out_6 : 30'bz;  // Controlled_Buffer controlled_buffer_5
  Pull_Resistor pull_resistor_6 (.node(pull_resistor_6_node));
  assign pull_resistor_6_node = divider_1_out[0] ? get_next_sprite_2_out_7 : 30'bz;  // Controlled_Buffer controlled_buffer_6
  Pull_Resistor pull_resistor_7 (.node(out_9));
  assign out_9 = in_1 ? controlled_buffer_1_out : 30'bz;  // Controlled_Buffer controlled_buffer_7
  Pull_Resistor pull_resistor_8 (.node(out_10));
  assign out_10 = in_1 ? controlled_buffer_2_out : 30'bz;  // Controlled_Buffer controlled_buffer_8
  assign out_11 = in_1 ? pull_resistor_3_node : 30'bz;  // Controlled_Buffer controlled_buffer_9
  Pull_Resistor pull_resistor_9 (.node(out_11));
  Pull_Resistor pull_resistor_10 (.node(out_12));
  assign out_12 = in_1 ? pull_resistor_4_node : 30'bz;  // Controlled_Buffer controlled_buffer_10
  Pull_Resistor pull_resistor_11 (.node(out_13));
  assign out_13 = in_1 ? pull_resistor_5_node : 30'bz;  // Controlled_Buffer controlled_buffer_11
  Pull_Resistor pull_resistor_12 (.node(out_14));
  assign out_14 = in_1 ? pull_resistor_6_node : 30'bz;  // Controlled_Buffer controlled_buffer_12

  // Notes on the sheet:
  //   GET SPRITE
endmodule

module ghost (
  input  [5:0] s_x,
  input  [5:0] s_y,
  input  [5:0] move_to_x,
  input  [5:0] move_to_y,
  input  loaded,
  input  reset,
  input  fruit,
  input  clock,
  output [8:0] out_9,
  output [5:0] out_10,
  output [5:0] out_11,
  output [4:0] player
);

  wire any_collision_detector_1_out_7, any_x, any_y, clk, collision, controlled_buffer_2_out,
       controlled_buffer_3_out, hunt, scatter, x_inc, y_inc;
  wire [3:2] move_to_1_move_to;
  wire [5:0] mtx, mty, random_1_out, random_2_out, transistor_3_out, transistor_4_out, x, x_q, y, y_q;
  wire [8:0] adder_3_out, bit_extender_1_out, bit_extender_2_out, multiplier_1_out;

  Transistor #(.\type ("n"), .gate("br"), .width(6)) transistor_1 (.in(random_1_out), .out(mtx), .gate(fruit));
  Random #(.width(6)) random_1 (.clk(clk), .out(random_1_out));  // open: next, clr
  Transistor #(.\type ("n"), .width(6)) transistor_2 (.in(random_2_out), .out(mty), .gate(fruit));
  Random #(.width(6)) random_2 (.clk(clk), .out(random_2_out));  // open: next, clr
  Pull_Resistor pull_resistor_1 (.node(s_x));
  Pull_Resistor pull_resistor_2 (.node(s_y));
  Transistor #(.\type ("n"), .gate("br"), .width(6)) transistor_3 (.in(s_x), .out(transistor_3_out), .gate(scatter));
  Transistor #(.\type ("n"), .width(6)) transistor_4 (.in(s_y), .out(transistor_4_out), .gate(scatter));
  Transistor #(.\type ("n"), .gate("br"), .width(6)) transistor_5 (.in(move_to_x), .out(transistor_3_out), .gate(hunt));
  Transistor #(.\type ("n"), .width(6)) transistor_6 (.in(move_to_y), .out(transistor_4_out), .gate(hunt));
  Transistor #(.\type ("n")) transistor_7 (.in(clock), .out(clk), .gate(loaded));
  Multiplexer #(.width(5), .enable("false")) multiplexer_1 (.in0(5'b00100), .in1(5'b00101), .out(player), .sel(fruit));
  Transistor #(.gate("br"), .width(6)) transistor_8 (.in(transistor_3_out), .out(mtx), .gate(fruit));
  Transistor #(.width(6)) transistor_9 (.in(transistor_4_out), .out(mty), .gate(fruit));
  any_collision_detector any_collision_detector_1 (
    .x(x), .y(y), .x_inc(x_inc), .y_inc(y_inc), .any_x(any_x), .any_y(any_y),
    .out_7(any_collision_detector_1_out_7));  // open: out_8, out_9
  current_mode current_mode_1 (.fruit(fruit), .hunt(hunt), .scatter(scatter), .clk(clk), .reset(reset));
  not not_1 (collision, any_collision_detector_1_out_7);
  assign out_10 = clk ? x : 6'bz;  // Controlled_Buffer controlled_buffer_1
  assign controlled_buffer_2_out = any_x ? clk : 1'bz;  // Controlled_Buffer controlled_buffer_2
  assign controlled_buffer_3_out = any_y ? clk : 1'bz;  // Controlled_Buffer controlled_buffer_3
  assign out_11 = clk ? y : 6'bz;  // Controlled_Buffer controlled_buffer_4
  Counter #(.width(6), .max('h13)) u_x (
    .load(x_inc), .Q(x_q), .clk(controlled_buffer_2_out), .clr(reset));  // open: D, count, carry
  Adder #(.width(6)) adder_1 (.a(x_q), .b({6{1'b0}}), .out(x));  // open: cin, cout
  Adder #(.width(6)) adder_2 (.a({6{1'b0}}), .b(y_q), .out(y));  // open: cin, cout
  Counter #(.width(6), .max('h13)) u_y (
    .load(y_inc), .Q(y_q), .clk(controlled_buffer_3_out), .clr(reset));  // open: D, count, carry
  move_to move_to_1 (
    .move_to_x(mtx), .move_to_y(mty), .curr_x(x), .curr_y(y), .move_to({move_to_1_move_to, x_inc, y_inc}),
    .start(clk));
  assign bit_extender_1_out = {{3{x[5]}}, x};  // Bit_Extender bit_extender_1
  assign bit_extender_2_out = {{3{y[5]}}, y};  // Bit_Extender bit_extender_2
  Pull_Resistor pull_resistor_3 (.node(y_inc));
  Pull_Resistor pull_resistor_4 (.node(move_to_1_move_to[3]));
  Pull_Resistor pull_resistor_5 (.node(move_to_1_move_to[2]));
  Pull_Resistor pull_resistor_6 (.node(x_inc));
  Adder #(.width(9)) adder_3 (.a(bit_extender_1_out), .b(multiplier_1_out), .out(adder_3_out));  // open: cin, cout
  assign out_9 = clk ? adder_3_out : 9'bz;  // Controlled_Buffer controlled_buffer_5
  Pull_Resistor pull_resistor_7 (.node(out_9));
  Multiplier #(.width(9)) multiplier_1 (.a(9'h14), .b(bit_extender_2_out), .out(multiplier_1_out));  // open: cin, cout
  or or_1 (any_y, y_inc, move_to_1_move_to[2]);
  or or_2 (any_x, x_inc, move_to_1_move_to[3]);

  // Notes on the sheet:
  //   input
  //   sprite handler
  //   collision detector
  //   mode chooser
  //   GHOST
  //   movement
  //   xy position
endmodule

module any_collision_detector (
  input  [5:0] x,
  input  x_inc,
  input  any_x,
  input  [5:0] y,
  input  y_inc,
  input  any_y,
  output out_7,
  output [5:0] out_8,
  output [5:0] out_9
);

  wire collision_detector_1_out_2, not_1_out, not_2_out, not_3_out, not_4_out;
  wire [2:0] sprite_dict_1_out_2, sprite_dict_1_out_3, sprite_dict_1_out_4;
  wire [4:0] map_handler_1_out_3;
  wire [5:0] adder_1_out, adder_2_out, controlled_buffer_1_out, controlled_buffer_5_out, subtractor_1_out,
       subtractor_2_out;

  Adder #(.width(6)) adder_1 (.a(x), .b(6'b000001), .out(adder_1_out));  // open: cin, cout
  Subtractor #(.width(6)) subtractor_1 (.a(x), .b(6'b000001), .out(subtractor_1_out));  // open: bin, bout
  Adder #(.width(6)) adder_2 (.a(y), .b(6'b000001), .out(adder_2_out));  // open: cin, cout
  Subtractor #(.width(6)) subtractor_2 (.a(y), .b(6'b000001), .out(subtractor_2_out));  // open: bin, bout
  assign controlled_buffer_1_out = not_1_out ? adder_1_out : 6'bz;  // Controlled_Buffer controlled_buffer_1
  not not_1 (not_1_out, x_inc);
  assign controlled_buffer_1_out = x_inc ? subtractor_1_out : 6'bz;  // Controlled_Buffer controlled_buffer_2
  assign out_8 = any_x ? controlled_buffer_1_out : 6'bz;  // Controlled_Buffer controlled_buffer_3
  assign out_8 = not_2_out ? x : 6'bz;  // Controlled_Buffer controlled_buffer_4
  not not_2 (not_2_out, any_x);
  assign controlled_buffer_5_out = not_3_out ? adder_2_out : 6'bz;  // Controlled_Buffer controlled_buffer_5
  not not_3 (not_3_out, y_inc);
  assign controlled_buffer_5_out = y_inc ? subtractor_2_out : 6'bz;  // Controlled_Buffer controlled_buffer_6
  assign out_9 = any_y ? controlled_buffer_5_out : 6'bz;  // Controlled_Buffer controlled_buffer_7
  not not_4 (not_4_out, any_y);
  sprite_dict sprite_dict_1 (
    .in_1(map_handler_1_out_3), .out_2(sprite_dict_1_out_2), .out_3(sprite_dict_1_out_3),
    .out_4(sprite_dict_1_out_4));
  DotMatrix #(.inputtype("row"), .matrixcols(3), .matrixrows(3)) dotmatrix_1 (
    .row0(sprite_dict_1_out_2), .row1(sprite_dict_1_out_3), .row2(sprite_dict_1_out_4));
  map_handler map_handler_1 (.x(out_8), .y(out_9), .out_3(map_handler_1_out_3));
  collision_detector collision_detector_1 (.out_2(collision_detector_1_out_2), .in_1(map_handler_1_out_3));
  assign out_9 = not_4_out ? y : 6'bz;  // Controlled_Buffer controlled_buffer_8
  not not_5 (out_7, collision_detector_1_out_2);

  // Notes on the sheet:
  //   COLLISION DETECTOR
endmodule

module intel_core_pentium (
  input  [6:0] all_entities,
  input  in_2,
  input  [2:0] in_3,
  input  [2:0] in_4,
  input  [2:0] in_5,
  input  [2:0] in_6,
  input  [2:0] in_7,
  input  [2:0] in_8,
  input  reset,
  output [8:0] index,
  output [15:0] data,
  output loaded,
  output pacman,
  output clock,
  output draw,
  output out_16,
  output out_17,
  output out_18,
  output out_19,
  output out_20
);

  wire active, Blinky, cdm16_1_p5, cdm16_1_p6, cdm16_1_p7, clk, Clyde, comparator_1_eq, Inky, not_1_out,
       not_2_out, Pinky, player_1_fruit, ram, read, rom, transistor_1_out, transistor_18_out, word;
  wire [2:0] counter_2_q, transistor_26_out;
  wire [4:0] ghost_1_player, ghost_2_player, ghost_3_player, ghost_4_player, player_1_player,
       transistor_11_out;
  wire [5:0] ghost_1_out_10, ghost_1_out_11, player_1_out_21, player_1_out_22;
  wire [8:0] ghost_1_out_9, ghost_2_out_9, ghost_3_out_9, ghost_4_out_9, player_1_out_15, transistor_2_out,
       vec_adr;
  wire [15:0] adder_1_out, addr, all_data, Bdata, bit_extender_2_out, cdm16_1_p8, cdm16_1_p9, cdm16_1_p10,
       r1, r5, rom_1_p4, transistor_19_out;

  // cdm16 cdm16_1: pin names not known; wires that end beside it: active, r1, clk, r5, cdm16_1_p5, cdm16_1_p6, cdm16_1_p7, cdm16_1_p8, cdm16_1_p9, cdm16_1_p10
  Clock clock_1 (.out(clk));
  assign Bdata = not_1_out ? cdm16_1_p9 : 16'bz;  // Controlled_Buffer controlled_buffer_1
  not not_1 (not_1_out, read);
  assign cdm16_1_p10 = read ? Bdata : 16'bz;  // Controlled_Buffer controlled_buffer_2
  Transistor transistor_1 (.in(cdm16_1_p5), .out(transistor_1_out), .gate(active));
  Decoder #(.enable("false")) decoder_1 (.out0(rom), .out1(ram), .sel(transistor_1_out));
  Transistor #(.\type ("n"), .width(9)) transistor_2 (.in(player_1_out_15), .out(transistor_2_out), .gate(pacman));
  player player_1 (
    .in_4(all_entities), .out_15(player_1_out_15), .player(player_1_player), .clock(pacman), .out_17(out_17),
    .reset(reset), .out_21(player_1_out_21), .out_22(player_1_out_22), .out_16(out_18), .in_6(in_2),
    .fruit(player_1_fruit), .g_x(ghost_1_out_10), .g_y(ghost_1_out_11), .out_18(out_20), .out_14(out_19),
    .in_3(in_3), .in_5(in_6), .in_8(in_4), .in_11(in_5), .in_12(in_8), .in_10(in_7), .loaded(loaded));
  Transistor #(.\type ("n"), .width(9)) transistor_3 (.in(ghost_1_out_9), .out(transistor_2_out), .gate(Blinky));
  ghost ghost_1 (
    .s_x({6{1'b0}}), .s_y({6{1'b0}}), .move_to_x(player_1_out_22), .move_to_y(player_1_out_21),
    .fruit(player_1_fruit), .reset(reset), .clock(Blinky), .out_9(ghost_1_out_9), .player(ghost_1_player),
    .out_10(ghost_1_out_10), .out_11(ghost_1_out_11), .loaded(loaded));
  Transistor #(.\type ("n"), .width(9)) transistor_4 (.in(ghost_2_out_9), .out(transistor_2_out), .gate(Pinky));
  ghost ghost_2 (
    .s_x({6{1'b0}}), .s_y(6'b010100), .move_to_x(player_1_out_22), .move_to_y(player_1_out_21),
    .fruit(player_1_fruit), .reset(reset), .clock(Pinky), .out_9(ghost_2_out_9), .player(ghost_2_player),
    .out_10(ghost_1_out_10), .out_11(ghost_1_out_11), .loaded(loaded));
  Transistor #(.\type ("n"), .width(9)) transistor_5 (.in(ghost_3_out_9), .out(transistor_2_out), .gate(Inky));
  ghost ghost_3 (
    .s_x(6'b010100), .s_y({6{1'b0}}), .move_to_x(player_1_out_22), .move_to_y(player_1_out_21),
    .fruit(player_1_fruit), .reset(reset), .clock(Inky), .out_9(ghost_3_out_9), .player(ghost_3_player),
    .out_10(ghost_1_out_10), .out_11(ghost_1_out_11), .loaded(loaded));
  Transistor #(.\type ("n"), .width(9)) transistor_6 (.in(ghost_4_out_9), .out(transistor_2_out), .gate(Clyde));
  ghost ghost_4 (
    .s_x(6'b010100), .s_y(6'b010100), .move_to_x(player_1_out_22), .move_to_y(player_1_out_21),
    .fruit(player_1_fruit), .reset(reset), .clock(Clyde), .out_9(ghost_4_out_9), .player(ghost_4_player),
    .out_10(ghost_1_out_10), .out_11(ghost_1_out_11), .loaded(loaded));
  Transistor #(.\type ("n")) transistor_7 (.in(1'b1), .out(read), .gate(active));
  Transistor transistor_8 (.in(cdm16_1_p6), .out(read), .gate(active));
  Transistor transistor_9 (.in(cdm16_1_p7), .out(word), .gate(active));
  Transistor #(.width(16)) transistor_10 (.in(cdm16_1_p8), .out(addr), .gate(active));
  Pull_Resistor pull_resistor_1 (.node(transistor_2_out));
  Transistor #(.\type ("n"), .width(5)) transistor_11 (.in(player_1_player), .out(transistor_11_out), .gate(pacman));
  Transistor #(.\type ("n"), .width(5)) transistor_12 (.in(ghost_1_player), .out(transistor_11_out), .gate(Blinky));
  Transistor #(.\type ("n"), .width(5)) transistor_13 (.in(ghost_2_player), .out(transistor_11_out), .gate(Pinky));
  Transistor #(.\type ("n"), .width(5)) transistor_14 (.in(ghost_3_player), .out(transistor_11_out), .gate(Inky));
  Transistor #(.\type ("n"), .width(5)) transistor_15 (.in(ghost_4_player), .out(transistor_11_out), .gate(Clyde));
  Transistor #(.\type ("n")) transistor_16 (.in(1'b1), .out(ram), .gate(active));
  Transistor #(.\type ("n"), .gate("br"), .width(9)) transistor_17 (.in(transistor_2_out), .out(index), .gate(loaded));
  assign all_data = {{11{1'b0}}, transistor_11_out};  // Bit_Extender bit_extender_1
  Pull_Resistor pull_resistor_2 (.node(all_data));
  Register #(.width(1)) register_1 (.D(loaded), .Q(active), .clk(loaded));  // open: en, clr
  not not_2 (not_2_out, loaded);
  Transistor #(.\type ("n")) transistor_18 (.in(clk), .out(transistor_18_out), .gate(active));
  Comparator #(.width(16), .mode("unsigned")) comparator_1 (.a(16'h1), .b(r5), .eq(comparator_1_eq));  // open: gt, lt
  Transistor #(.\type ("n"), .gate("br"), .width(16)) transistor_19 (
    .in(Bdata), .out(transistor_19_out), .gate(active));
  Transistor #(.width(16)) transistor_20 (.in(r1), .out(transistor_19_out), .gate(active));
  Counter #(.width(9), .max('h190), .trigger("falling")) counter_1 (
    .count(not_2_out), .Q(vec_adr), .carry(loaded), .clk(transistor_18_out), .clr(reset));  // open: load, D
  Counter #(.width(3), .max('h6)) counter_2 (.Q(counter_2_q), .carry(draw), .clk(clock));  // open: load, D, count, clr
  Transistor #(.gate("br")) transistor_21 (.in(comparator_1_eq), .out(transistor_18_out), .gate(active));
  Transistor #(.gate("br")) transistor_22 (.in(comparator_1_eq), .out(clock), .gate(active));
  Transistor #(.\type ("n")) transistor_23 (.in(clk), .out(clock), .gate(active));
  Transistor #(.gate("br"), .width(16)) transistor_24 (.in(transistor_19_out), .out(data), .gate(loaded));
  Transistor #(.width(9)) transistor_25 (.in(vec_adr), .out(index), .gate(loaded));
  Transistor #(.\type ("n"), .width(3)) transistor_26 (.in(counter_2_q), .out(transistor_26_out), .gate(loaded));
  Pull_Resistor #(.pull(1)) pull_resistor_3 (.node(transistor_26_out));
  Decoder #(.select(3), .disabled(0), .enable("false")) decoder_2 (
    .out0(Blinky), .out1(Pinky), .out2(Inky), .out3(Clyde), .out4(pacman), .sel(transistor_26_out));  // open: out5, out6, out7
  Transistor #(.\type ("n"), .gate("br"), .width(16)) transistor_27 (.in(all_data), .out(data), .gate(loaded));
  assign bit_extender_2_out = {{7{1'b0}}, vec_adr};  // Bit_Extender bit_extender_2
  Adder #(.width(16)) adder_1 (.a(bit_extender_2_out), .b(16'h8a), .out(adder_1_out));  // open: cin, cout
  Transistor #(.\type ("n"), .width(16)) transistor_28 (.in(adder_1_out), .out(addr), .gate(active));
  // ROM rom_1: pin names not known; wires that end beside it: addr, rom, word, rom_1_p4
  Transistor #(.width(16)) transistor_29 (.in(rom_1_p4), .out(Bdata), .gate(active));
  // RAM ram_1: pin names not known; wires that end beside it: addr, word, ram, clk, read

  assign out_16 = reset;

  // Other names for the same wires on the sheet: dtb[8:0] = index; player = pacman; t1[2:0] = in_3; t2[2:0] = in_6;
  //   t3[2:0] = in_4; t4[2:0] = in_7; t5[2:0] = in_5; t6[2:0] = in_8

  // Notes on the sheet:
  //   CdM-16 processor
  //   CORE
  //   input
  //   result handler
  //   memory
endmodule

module move_to (
  input  start,
  input  [5:0] move_to_x,
  input  [5:0] curr_x,
  input  [5:0] move_to_y,
  input  [5:0] curr_y,
  output [3:0] move_to
);

  wire any_collision_detector_1_out_7, any_collision_detector_2_out_7, any_collision_detector_3_out_7,
       any_collision_detector_4_out_7, comparator_1_eq, comparator_1_gt, comparator_1_lt, comparator_2_eq,
       comparator_2_gt, comparator_2_lt, comparator_3_eq, comparator_3_gt, comparator_3_lt, down, left,
       not_1_out, not_2_out, not_3_out, not_4_out, or_1_out, or_2_out, or_3_out, or_4_out, or_5_out, right,
       up;
  wire [3:0] controlled_buffer_7_out, register_1_q, xor_1_out, xor_2_out;
  wire [5:0] downx, downy, leftx, lefty, rightx, righty, upx, upy;
  wire [31:0] controlled_buffer_1_out, controlled_buffer_3_out, controlled_buffer_5_out, distance_1_out_6,
       distance_2_out_6, distance_3_out_6, distance_4_out_6;

  distance distance_1 (
    .move_to_x(move_to_x), .move_to_y(move_to_y), .curr_x(upx), .curr_y(upy), .out_6(distance_1_out_6),
    .active(up));
  Comparator #(.width(32), .mode("unsigned")) comparator_1 (
    .a(distance_1_out_6), .b(distance_2_out_6), .gt(comparator_1_gt), .eq(comparator_1_eq),
    .lt(comparator_1_lt));
  distance distance_2 (
    .move_to_x(move_to_x), .move_to_y(move_to_y), .curr_x(leftx), .curr_y(lefty), .out_6(distance_2_out_6),
    .active(left));
  distance distance_3 (
    .move_to_x(move_to_x), .move_to_y(move_to_y), .curr_x(downx), .curr_y(downy), .out_6(distance_3_out_6),
    .active(down));
  Comparator #(.width(32), .mode("unsigned")) comparator_2 (
    .a(distance_3_out_6), .b(distance_4_out_6), .gt(comparator_2_gt), .eq(comparator_2_eq),
    .lt(comparator_2_lt));
  distance distance_4 (
    .move_to_x(move_to_x), .move_to_y(move_to_y), .curr_x(rightx), .curr_y(righty), .out_6(distance_4_out_6),
    .active(right));
  assign controlled_buffer_1_out = or_1_out ? distance_1_out_6 : 32'bz;  // Controlled_Buffer controlled_buffer_1
  or or_1 (or_1_out, comparator_1_eq, comparator_1_lt);
  assign controlled_buffer_1_out = comparator_1_gt ? distance_2_out_6 : 32'bz;  // Controlled_Buffer controlled_buffer_2
  assign controlled_buffer_3_out = or_2_out ? distance_3_out_6 : 32'bz;  // Controlled_Buffer controlled_buffer_3
  or or_2 (or_2_out, comparator_2_eq, comparator_2_lt);
  assign controlled_buffer_3_out = comparator_2_gt ? distance_4_out_6 : 32'bz;  // Controlled_Buffer controlled_buffer_4
  Comparator #(.width(32), .mode("unsigned")) comparator_3 (
    .a(controlled_buffer_1_out), .b(controlled_buffer_3_out), .gt(comparator_3_gt), .eq(comparator_3_eq),
    .lt(comparator_3_lt));
  assign controlled_buffer_5_out = comparator_3_gt ? controlled_buffer_3_out : 32'bz;  // Controlled_Buffer controlled_buffer_5
  and and_1 (move_to[0], or_1_out, or_3_out);
  and and_2 (move_to[1], comparator_1_gt, or_3_out);
  assign controlled_buffer_5_out = or_3_out ? controlled_buffer_1_out : 32'bz;  // Controlled_Buffer controlled_buffer_6
  or or_3 (or_3_out, comparator_3_eq, comparator_3_lt);
  and and_3 (move_to[2], comparator_3_gt, or_2_out);
  and and_4 (move_to[3], comparator_3_gt, comparator_2_gt);
  or or_4 (or_4_out, move_to[0], move_to[2]);
  assign controlled_buffer_7_out = or_4_out ? xor_1_out : 4'bz;  // Controlled_Buffer controlled_buffer_7
  assign xor_1_out = 4'b0101 ^ move_to;  // XOR_Gate xor_1, 4 bits wide
  Pull_Resistor pull_resistor_1 (.node(controlled_buffer_7_out));
  assign xor_2_out = move_to ^ 4'b1010;  // XOR_Gate xor_2, 4 bits wide
  assign controlled_buffer_7_out = or_5_out ? xor_2_out : 4'bz;  // Controlled_Buffer controlled_buffer_8
  or or_5 (or_5_out, move_to[1], move_to[3]);
  Register #(.width(4)) register_1 (.D(controlled_buffer_7_out), .Q(register_1_q), .clk(start));  // open: en, clr
  Pull_Resistor pull_resistor_2 (.node(register_1_q[0]));
  Pull_Resistor pull_resistor_3 (.node(register_1_q[1]));
  Pull_Resistor pull_resistor_4 (.node(register_1_q[2]));
  Pull_Resistor pull_resistor_5 (.node(register_1_q[3]));
  not not_1 (not_1_out, register_1_q[3]);
  any_collision_detector any_collision_detector_1 (
    .x(curr_x), .y(curr_y), .x_inc(1'b0), .y_inc(1'b0), .any_x(1'b1), .any_y(1'b0),
    .out_7(any_collision_detector_1_out_7), .out_8(rightx), .out_9(righty));
  assign right = not_1_out ? any_collision_detector_1_out_7 : 1'bz;  // Controlled_Buffer controlled_buffer_9
  Pull_Resistor pull_resistor_6 (.node(right));
  assign up = not_2_out ? any_collision_detector_2_out_7 : 1'bz;  // Controlled_Buffer controlled_buffer_10
  any_collision_detector any_collision_detector_2 (
    .x(curr_x), .y(curr_y), .x_inc(1'b0), .y_inc(1'b1), .any_x(1'b0), .any_y(1'b1),
    .out_7(any_collision_detector_2_out_7), .out_8(upx), .out_9(upy));
  Pull_Resistor pull_resistor_7 (.node(up));
  not not_2 (not_2_out, register_1_q[0]);
  not not_3 (not_3_out, register_1_q[2]);
  any_collision_detector any_collision_detector_3 (
    .x(curr_x), .y(curr_y), .x_inc(1'b0), .y_inc(1'b0), .any_x(1'b0), .any_y(1'b1),
    .out_7(any_collision_detector_3_out_7), .out_8(downx), .out_9(downy));
  assign down = not_3_out ? any_collision_detector_3_out_7 : 1'bz;  // Controlled_Buffer controlled_buffer_11
  Pull_Resistor pull_resistor_8 (.node(down));
  not not_4 (not_4_out, register_1_q[1]);
  assign left = not_4_out ? any_collision_detector_4_out_7 : 1'bz;  // Controlled_Buffer controlled_buffer_12
  Pull_Resistor pull_resistor_9 (.node(left));
  any_collision_detector any_collision_detector_4 (
    .x(curr_x), .y(curr_y), .x_inc(1'b1), .y_inc(1'b0), .any_x(1'b1), .any_y(1'b0),
    .out_7(any_collision_detector_4_out_7), .out_8(leftx), .out_9(lefty));

  // Other names for the same wires on the sheet: mtx[5:0] = move_to_x; mty[5:0] = move_to_y; x[5:0] = curr_x;
  //   y[5:0] = curr_y

  // Notes on the sheet:
  //   MOVE TO
endmodule

module distance (
  input  [5:0] curr_x,
  input  [5:0] curr_y,
  input  active,
  input  [5:0] move_to_x,
  input  [5:0] move_to_y,
  output [31:0] out_6
);

  wire subtractor_1_bout, subtractor_2_bout;
  wire [5:0] negator_1_out, negator_2_out, subtractor_1_out, subtractor_2_out, transistor_1_out,
       transistor_3_out;
  wire [31:0] adder_1_out, bit_extender_1_out, bit_extender_2_out, multiplier_1_out, multiplier_2_out;

  Subtractor #(.width(6)) subtractor_1 (
    .a(curr_x), .b(move_to_x), .out(subtractor_1_out), .bout(subtractor_1_bout));  // open: bin
  Subtractor #(.width(6)) subtractor_2 (
    .a(move_to_y), .b(curr_y), .out(subtractor_2_out), .bout(subtractor_2_bout));  // open: bin
  Transistor #(.\type ("n"), .width(6)) transistor_1 (
    .in(negator_1_out), .out(transistor_1_out), .gate(subtractor_1_bout));
  Transistor #(.gate("br"), .width(6)) transistor_2 (
    .in(subtractor_1_out), .out(transistor_1_out), .gate(subtractor_1_bout));
  Negator #(.width(6)) negator_1 (.in(subtractor_1_out), .out(negator_1_out));
  Transistor #(.\type ("n"), .width(6)) transistor_3 (
    .in(negator_2_out), .out(transistor_3_out), .gate(subtractor_2_bout));
  Transistor #(.gate("br"), .width(6)) transistor_4 (
    .in(subtractor_2_out), .out(transistor_3_out), .gate(subtractor_2_bout));
  Negator #(.width(6)) negator_2 (.in(subtractor_2_out), .out(negator_2_out));
  assign bit_extender_1_out = {{26{1'b0}}, transistor_1_out};  // Bit_Extender bit_extender_1
  Multiplier #(.width(32)) multiplier_1 (
    .a(bit_extender_1_out), .b(bit_extender_1_out), .out(multiplier_1_out));  // open: cin, cout
  assign bit_extender_2_out = {{26{1'b0}}, transistor_3_out};  // Bit_Extender bit_extender_2
  Multiplier #(.width(32)) multiplier_2 (
    .a(bit_extender_2_out), .b(bit_extender_2_out), .out(multiplier_2_out));  // open: cin, cout
  Adder #(.width(32)) adder_1 (.a(multiplier_1_out), .b(multiplier_2_out), .out(adder_1_out));  // open: cin, cout
  assign out_6 = active ? adder_1_out : 32'bz;  // Controlled_Buffer controlled_buffer_1
  Pull_Resistor #(.pull(1)) pull_resistor_1 (.node(out_6));

  // Other names for the same wires on the sheet: mtx[5:0] = move_to_x; mty[5:0] = move_to_y; x[5:0] = curr_x;
  //   y[5:0] = curr_y

  // Notes on the sheet:
  //   DISTANCE
endmodule
